// Logisim project 1.circ as structural Verilog: 54 circuits, main circuit minirv
module Decoder2_4 (
  input  A0,
  input  A1,
  input  enable,
  output Y0,
  output Y1,
  output Y2,
  output Y3
);

  wire not_1_out, not_2_out;

  not not_1 (not_1_out, A0);
  not not_2 (not_2_out, A1);
  and and_1 (Y0, not_1_out, enable, not_2_out);
  and and_2 (Y1, A0, enable, not_2_out);
  and and_3 (Y2, not_1_out, enable, A1);
  and and_4 (Y3, A1, enable, A0);
endmodule

module Decoder3_8 (
  input  A0,
  input  A1,
  input  A2,
  input  enable,
  output Y0,
  output Y1,
  output Y2,
  output Y3,
  output Y4,
  output Y5,
  output Y6,
  output Y7
);

  wire decoder2_4_1_y0, decoder2_4_1_y1, decoder2_4_1_y2, decoder2_4_1_y3, decoder2_4_2_y0, decoder2_4_2_y1,
       decoder2_4_2_y2, decoder2_4_2_y3, not_1_out;

  not not_1 (not_1_out, A2);
  Decoder2_4 decoder2_4_1 (
    .A0(A0), .A1(A1), .enable(A2), .Y0(decoder2_4_1_y0), .Y1(decoder2_4_1_y1), .Y2(decoder2_4_1_y2),
    .Y3(decoder2_4_1_y3));
  Decoder2_4 decoder2_4_2 (
    .A0(A0), .A1(A1), .enable(not_1_out), .Y0(decoder2_4_2_y0), .Y1(decoder2_4_2_y1), .Y2(decoder2_4_2_y2),
    .Y3(decoder2_4_2_y3));
  and and_1 (Y0, decoder2_4_2_y0, enable);
  and and_2 (Y1, decoder2_4_2_y1, enable);
  and and_3 (Y2, decoder2_4_2_y2, enable);
  and and_4 (Y3, decoder2_4_2_y3, enable);
  and and_5 (Y4, decoder2_4_1_y0, enable);
  and and_6 (Y5, decoder2_4_1_y1, enable);
  and and_7 (Y6, decoder2_4_1_y2, enable);
  and and_8 (Y7, decoder2_4_1_y3, enable);
endmodule

module Decoder4_16 (
  input  A0,
  input  A1,
  input  A2,
  input  A3,
  output out_5,
  output out_6,
  output out_7,
  output out_8,
  output out_9,
  output out_10,
  output out_11,
  output out_12,
  output out_13,
  output out_14,
  output out_15,
  output out_16,
  output out_17,
  output out_18,
  output out_19,
  output out_20
);

  wire not_1_out;

  not not_1 (not_1_out, A3);
  Decoder3_8 decoder3_8_1 (
    .A0(A0), .A1(A1), .A2(A2), .enable(not_1_out), .Y0(out_5), .Y1(out_6), .Y2(out_7), .Y3(out_8),
    .Y4(out_9), .Y5(out_10), .Y6(out_11), .Y7(out_12));
  Decoder3_8 decoder3_8_2 (
    .A0(A0), .A1(A1), .A2(A2), .enable(A3), .Y0(out_13), .Y1(out_14), .Y2(out_15), .Y3(out_16), .Y4(out_17),
    .Y5(out_18), .Y6(out_19), .Y7(out_20));
endmodule

module segment_7_0to9 (
  input  A0,
  input  A1,
  input  A2,
  input  A3,
  output S0,
  output S1,
  output S2,
  output S3,
  output X0,
  output X1,
  output X2,
  output X3
);

  wire decoder4_16_1_out_5, decoder4_16_1_out_6, decoder4_16_1_out_7, decoder4_16_1_out_8,
       decoder4_16_1_out_9, decoder4_16_1_out_10, decoder4_16_1_out_11, decoder4_16_1_out_12,
       decoder4_16_1_out_13, decoder4_16_1_out_14, decoder4_16_1_out_15, decoder4_16_1_out_16,
       decoder4_16_1_out_17, decoder4_16_1_out_18, decoder4_16_1_out_19, decoder4_16_1_out_20;

  Decoder4_16 decoder4_16_1 (
    .A0(A0), .A1(A1), .A2(A2), .A3(A3), .out_5(decoder4_16_1_out_5), .out_6(decoder4_16_1_out_6),
    .out_7(decoder4_16_1_out_7), .out_8(decoder4_16_1_out_8), .out_9(decoder4_16_1_out_9),
    .out_10(decoder4_16_1_out_10), .out_11(decoder4_16_1_out_11), .out_12(decoder4_16_1_out_12),
    .out_13(decoder4_16_1_out_13), .out_14(decoder4_16_1_out_14), .out_15(decoder4_16_1_out_15),
    .out_16(decoder4_16_1_out_16), .out_17(decoder4_16_1_out_17), .out_18(decoder4_16_1_out_18),
    .out_19(decoder4_16_1_out_19), .out_20(decoder4_16_1_out_20));
  or or_1 (S3, decoder4_16_1_out_5, decoder4_16_1_out_6, decoder4_16_1_out_7, decoder4_16_1_out_8, decoder4_16_1_out_9, decoder4_16_1_out_12, decoder4_16_1_out_13, decoder4_16_1_out_14);
  or or_2 (S2, decoder4_16_1_out_5, decoder4_16_1_out_7, decoder4_16_1_out_8, decoder4_16_1_out_12, decoder4_16_1_out_13, decoder4_16_1_out_10, decoder4_16_1_out_11, decoder4_16_1_out_14);
  or or_3 (X0, decoder4_16_1_out_5, decoder4_16_1_out_7, decoder4_16_1_out_11, decoder4_16_1_out_13);
  or or_4 (X2, decoder4_16_1_out_5, decoder4_16_1_out_6, decoder4_16_1_out_9, decoder4_16_1_out_8, decoder4_16_1_out_13, decoder4_16_1_out_10, decoder4_16_1_out_11, decoder4_16_1_out_12, decoder4_16_1_out_14);
  or or_5 (S1, decoder4_16_1_out_14, decoder4_16_1_out_5, decoder4_16_1_out_10, decoder4_16_1_out_9, decoder4_16_1_out_13, decoder4_16_1_out_11);
  or or_6 (X1, decoder4_16_1_out_10, decoder4_16_1_out_5, decoder4_16_1_out_7, decoder4_16_1_out_11, decoder4_16_1_out_13, decoder4_16_1_out_14, decoder4_16_1_out_8);
  or or_7 (S0, decoder4_16_1_out_14, decoder4_16_1_out_10, decoder4_16_1_out_8, decoder4_16_1_out_7, decoder4_16_1_out_11, decoder4_16_1_out_13, decoder4_16_1_out_9);
  or or_8 (X3, decoder4_16_1_out_15, decoder4_16_1_out_16, decoder4_16_1_out_17, decoder4_16_1_out_18, decoder4_16_1_out_19, decoder4_16_1_out_20);
endmodule

module segment_7_0toF (
  input  A0,
  input  A1,
  input  A2,
  input  A3,
  output S0,
  output S1,
  output S2,
  output S3,
  output X0,
  output X1,
  output X2,
  output X3
);

  wire decoder4_16_1_out_5, decoder4_16_1_out_6, decoder4_16_1_out_7, decoder4_16_1_out_8,
       decoder4_16_1_out_9, decoder4_16_1_out_10, decoder4_16_1_out_11, decoder4_16_1_out_12,
       decoder4_16_1_out_13, decoder4_16_1_out_14, decoder4_16_1_out_15, decoder4_16_1_out_16,
       decoder4_16_1_out_17, decoder4_16_1_out_18, decoder4_16_1_out_19, decoder4_16_1_out_20, or_1_out,
       or_2_out, or_3_out, or_4_out, or_6_out, or_7_out, or_8_out, or_9_out, or_11_out, or_12_out;

  Decoder4_16 decoder4_16_1 (
    .A0(A0), .A1(A1), .A2(A2), .A3(A3), .out_5(decoder4_16_1_out_5), .out_6(decoder4_16_1_out_6),
    .out_7(decoder4_16_1_out_7), .out_8(decoder4_16_1_out_8), .out_9(decoder4_16_1_out_9),
    .out_10(decoder4_16_1_out_10), .out_11(decoder4_16_1_out_11), .out_12(decoder4_16_1_out_12),
    .out_13(decoder4_16_1_out_13), .out_14(decoder4_16_1_out_14), .out_15(decoder4_16_1_out_15),
    .out_16(decoder4_16_1_out_16), .out_17(decoder4_16_1_out_17), .out_18(decoder4_16_1_out_18),
    .out_19(decoder4_16_1_out_19), .out_20(decoder4_16_1_out_20));
  or or_1 (or_1_out, decoder4_16_1_out_5, decoder4_16_1_out_7, decoder4_16_1_out_8, decoder4_16_1_out_12, decoder4_16_1_out_13, decoder4_16_1_out_10, decoder4_16_1_out_11, decoder4_16_1_out_14);
  or or_2 (or_2_out, decoder4_16_1_out_5, decoder4_16_1_out_7, decoder4_16_1_out_11, decoder4_16_1_out_13);
  or or_3 (or_3_out, decoder4_16_1_out_5, decoder4_16_1_out_6, decoder4_16_1_out_9, decoder4_16_1_out_8, decoder4_16_1_out_13, decoder4_16_1_out_10, decoder4_16_1_out_11, decoder4_16_1_out_12, decoder4_16_1_out_14);
  or or_4 (or_4_out, decoder4_16_1_out_15, decoder4_16_1_out_16, decoder4_16_1_out_17, decoder4_16_1_out_19, decoder4_16_1_out_20);
  or or_5 (S3, decoder4_16_1_out_15, decoder4_16_1_out_5, decoder4_16_1_out_6, decoder4_16_1_out_7, decoder4_16_1_out_8, decoder4_16_1_out_9, decoder4_16_1_out_12, decoder4_16_1_out_13, decoder4_16_1_out_14, decoder4_16_1_out_18);
  or or_6 (or_6_out, decoder4_16_1_out_14, decoder4_16_1_out_10, decoder4_16_1_out_8, decoder4_16_1_out_7, decoder4_16_1_out_11, decoder4_16_1_out_13, decoder4_16_1_out_9);
  or or_7 (or_7_out, decoder4_16_1_out_15, decoder4_16_1_out_16, decoder4_16_1_out_18, decoder4_16_1_out_19, decoder4_16_1_out_20);
  or or_8 (or_8_out, decoder4_16_1_out_15, decoder4_16_1_out_17, decoder4_16_1_out_19, decoder4_16_1_out_20);
  or or_9 (or_9_out, decoder4_16_1_out_16, decoder4_16_1_out_17, decoder4_16_1_out_18, decoder4_16_1_out_19);
  or or_10 (S2, or_1_out, or_8_out);
  or or_11 (or_11_out, decoder4_16_1_out_10, decoder4_16_1_out_5, decoder4_16_1_out_7, decoder4_16_1_out_11, decoder4_16_1_out_13, decoder4_16_1_out_14, decoder4_16_1_out_8);
  or or_12 (or_12_out, decoder4_16_1_out_14, decoder4_16_1_out_5, decoder4_16_1_out_10, decoder4_16_1_out_9, decoder4_16_1_out_13, decoder4_16_1_out_11);
  or or_13 (S0, or_6_out, or_7_out);
  or or_14 (S1, or_12_out, or_4_out);
  or or_15 (X1, or_9_out, or_11_out);
  or or_16 (X2, decoder4_16_1_out_15, decoder4_16_1_out_16, decoder4_16_1_out_18, or_3_out);
  _7_Segment_Display u_7_segment_display_1 ();  // open: g, f, a, b, e, d, c, dp
  or or_17 (X0, or_2_out, decoder4_16_1_out_17, decoder4_16_1_out_18, decoder4_16_1_out_16, or_8_out);
endmodule

module priority_encoder_4to2 (
  input  in_1,
  input  in_2,
  input  in_3,
  input  in_4,
  output out_5,
  output out_6
);

  wire and_1_out, not_1_out;

  not not_1 (not_1_out, in_3);
  and and_1 (and_1_out, not_1_out, in_2);
  or or_1 (out_5, and_1_out, in_4);
  or or_2 (out_6, in_3, in_4);
endmodule

module Encoder16_4 (
  input  A0,
  input  A1,
  input  A2,
  input  A3,
  input  A4,
  input  A5,
  input  A6,
  input  A7,
  input  A8,
  input  A9,
  input  A10,
  input  A11,
  input  A12,
  input  A13,
  input  A14,
  input  A15,
  output Y0,
  output Y1,
  output Y2,
  output Y3
);

  or or_1 (Y0, A1, A3, A5, A7, A9, A11, A13, A15);
  or or_2 (Y1, A15, A2, A6, A7, A10, A14, A11);
  or or_3 (Y2, A12, A13, A4, A5, A6, A7, A14, A15);
  or or_4 (Y3, A8, A9, A10, A11, A12, A13, A14, A15);
endmodule

module Mux2to1 (
  input  D0,
  input  S,
  input  D1,
  output Y
);

  wire and_1_out, and_2_out, not_1_out;

  not not_1 (not_1_out, S);
  and and_1 (and_1_out, D0, not_1_out);
  and and_2 (and_2_out, S, D1);
  or or_1 (Y, and_1_out, and_2_out);
endmodule

module Mux4to1_3bit (
  input  S0,
  input  S1,
  input  [2:0] A0,
  input  [2:0] A1,
  input  [2:0] A2,
  input  [2:0] A3,
  output [2:0] Y
);

  wire [2:0] and_1_out, and_2_out, and_3_out, and_4_out, not_1_out, not_2_out;

  assign not_1_out = ~{3{S0}};  // NOT_Gate not_1, 3 bits wide
  assign not_2_out = ~{3{S1}};  // NOT_Gate not_2, 3 bits wide
  assign and_1_out = not_1_out & A0 & not_2_out;  // AND_Gate and_1, 3 bits wide
  assign and_2_out = not_2_out & {3{S0}} & A1;  // AND_Gate and_2, 3 bits wide
  assign and_3_out = not_1_out & {3{S1}} & A2;  // AND_Gate and_3, 3 bits wide
  assign and_4_out = {3{S0}} & {3{S1}} & A3;  // AND_Gate and_4, 3 bits wide
  assign Y = and_1_out | and_2_out | and_3_out | and_4_out;  // OR_Gate or_1, 3 bits wide
endmodule

module comparator_4bit (
  input  [3:0] A,
  input  [3:0] B,
  output same
);

  wire [3:0] not_1_out, xor_1_out;

  assign xor_1_out = A ^ B;  // XOR_Gate xor_1, 4 bits wide
  assign not_1_out = ~xor_1_out;  // NOT_Gate not_1, 4 bits wide
  and and_1 (same, not_1_out[0], not_1_out[1], not_1_out[2], not_1_out[3]);
endmodule

module Add (
  input  A,
  input  B,
  input  Cin,
  output Sum,
  output Cout
);

  wire and_1_out, and_2_out, and_3_out;

  and and_1 (and_1_out, A, B);
  and and_2 (and_2_out, A, Cin);
  and and_3 (and_3_out, Cin, B);
  or or_1 (Cout, and_1_out, and_2_out, and_3_out);
  xor xor_1 (Sum, A, B, Cin);
endmodule

module Add_4bit (
  input  [3:0] A0,
  input  [3:0] A1,
  output Y0,
  output Y1,
  output Y2,
  output Y3,
  output Cout,
  output Overflow
);

  wire add_1_cout, add_2_cout, add_3_cout;

  Add add_1 (.A(A0[0]), .B(A1[0]), .Sum(Y0), .Cout(add_1_cout));  // open: Cin
  Add add_2 (.A(A0[1]), .B(A1[1]), .Cin(add_1_cout), .Sum(Y1), .Cout(add_2_cout));
  Add add_3 (.A(A0[2]), .B(A1[2]), .Cin(add_2_cout), .Sum(Y2), .Cout(add_3_cout));
  Add add_4 (.A(A0[3]), .B(A1[3]), .Cin(add_3_cout), .Sum(Y3), .Cout(Cout));
  xor xor_1 (Overflow, Cout, add_3_cout);
endmodule

module Sign_magnitude_adder_4bit (
  input  [3:0] A,
  input  [3:0] B,
  output Y0,
  output Y1,
  output Y2,
  output Y3
);

  wire add_4bit_1_y0, add_4bit_1_y1, add_4bit_1_y2, add_4bit_1_y3, and_1_out, and_6_out, and_7_out,
       mux2to1_4_y, nor_1_out, nor_2_out, not_1_out, not_3_out, segment_7_0to9_1_s0, segment_7_0to9_1_s1,
       segment_7_0to9_1_s2, segment_7_0to9_1_s3, segment_7_0to9_1_x0, segment_7_0to9_1_x1,
       segment_7_0to9_1_x2, sub_4bit_1_bout, sub_4bit_2_y0, sub_4bit_2_y1, sub_4bit_2_y2, sub_4bit_2_y3,
       xor_1_out;
  wire [3:0] and_2_out, and_3_out, and_4_out, and_5_out, not_2_out, or_1_out, or_2_out;
  wire [3:3] nor_3_out;

  not not_1 (not_1_out, 1'b0);
  and and_1 (and_1_out, not_1_out, A[3]);
  xor xor_1 (xor_1_out, A[3], B[3]);
  nor nor_1 (nor_1_out, A[3], B[3], 1'b0);
  nor nor_2 (nor_2_out, 1'b0, A[3]);
  assign not_2_out = ~{4{nor_3_out[3]}};  // NOT_Gate not_2, 4 bits wide
  assign and_2_out = {4{nor_3_out[3]}} & {1'b0, A[2:0]};  // AND_Gate and_2, 4 bits wide
  assign and_3_out = {4{nor_3_out[3]}} & {1'b0, B[2:0]};  // AND_Gate and_3, 4 bits wide
  Sub_4bit sub_4bit_1 (.A0({1'b0, A[2:0]}), .A1({1'b0, B[2:0]}), .Bout(sub_4bit_1_bout));  // open: Y0, Y1, Y2, Y3
  assign and_4_out = not_2_out & {1'b0, B[2:0]};  // AND_Gate and_4, 4 bits wide
  assign and_5_out = not_2_out & {1'b0, A[2:0]};  // AND_Gate and_5, 4 bits wide
  nor nor_3 (nor_3_out[3], sub_4bit_1_bout, 1'b0);
  assign or_1_out = and_2_out | and_4_out;  // OR_Gate or_1, 4 bits wide
  assign or_2_out = and_5_out | and_3_out;  // OR_Gate or_2, 4 bits wide
  Add_4bit add_4bit_1 (
    .A0(or_1_out), .A1(or_2_out), .Y0(add_4bit_1_y0), .Y1(add_4bit_1_y1), .Y2(add_4bit_1_y2),
    .Y3(add_4bit_1_y3));  // open: Cout, Overflow
  Sub_4bit sub_4bit_2 (
    .A0(or_1_out), .A1(or_2_out), .Y0(sub_4bit_2_y0), .Y1(sub_4bit_2_y1), .Y2(sub_4bit_2_y2),
    .Y3(sub_4bit_2_y3));  // open: Bout
  not not_3 (not_3_out, sub_4bit_1_bout);
  and and_6 (and_6_out, not_3_out, xor_1_out, nor_2_out);
  and and_7 (and_7_out, xor_1_out, and_1_out, sub_4bit_1_bout);
  Mux2to1 mux2to1_1 (.D0(add_4bit_1_y0), .S(xor_1_out), .D1(sub_4bit_2_y0), .Y(Y0));
  Mux2to1 mux2to1_2 (.D0(add_4bit_1_y1), .S(xor_1_out), .D1(sub_4bit_2_y1), .Y(Y1));
  Mux2to1 mux2to1_3 (.D0(add_4bit_1_y2), .S(xor_1_out), .D1(sub_4bit_2_y2), .Y(Y2));
  Mux2to1 mux2to1_4 (.D0(add_4bit_1_y3), .S(xor_1_out), .D1(sub_4bit_2_y3), .Y(mux2to1_4_y));
  nor nor_4 (Y3, and_6_out, nor_1_out, and_7_out);
  segment_7_0to9 segment_7_0to9_1 (
    .A0(Y0), .A1(Y1), .A2(Y2), .A3(mux2to1_4_y), .S0(segment_7_0to9_1_s0), .S1(segment_7_0to9_1_s1),
    .S2(segment_7_0to9_1_s2), .S3(segment_7_0to9_1_s3), .X0(segment_7_0to9_1_x0), .X1(segment_7_0to9_1_x1),
    .X2(segment_7_0to9_1_x2));  // open: X3
  _7_Segment_Display u_7_segment_display_1 (.g(Y3));  // open: f, a, b, e, d, c, dp
  _7_Segment_Display u_7_segment_display_2 (
    .g(segment_7_0to9_1_s0), .f(segment_7_0to9_1_s1), .a(segment_7_0to9_1_s2), .b(segment_7_0to9_1_s3),
    .e(segment_7_0to9_1_x0), .d(segment_7_0to9_1_x1), .c(segment_7_0to9_1_x2));  // open: dp
endmodule

module Sub (
  input  A,
  input  B,
  input  Bin,
  output Diff,
  output Bout
);

  wire and_1_out, and_2_out, and_3_out, not_1_out;

  not not_1 (not_1_out, A);
  xor xor_1 (Diff, A, B, Bin);
  and and_1 (and_1_out, not_1_out, B);
  and and_2 (and_2_out, not_1_out, Bin);
  and and_3 (and_3_out, Bin, B);
  or or_1 (Bout, and_1_out, and_2_out, and_3_out);
endmodule

module Sub_4bit (
  input  [3:0] A0,
  input  [3:0] A1,
  output Y0,
  output Y1,
  output Y2,
  output Y3,
  output Bout
);

  wire sub_1_bout, sub_2_bout, sub_3_bout;

  Sub sub_1 (.A(A0[0]), .B(A1[0]), .Diff(Y0), .Bout(sub_1_bout));  // open: Bin
  Sub sub_2 (.A(A0[1]), .B(A1[1]), .Bin(sub_1_bout), .Diff(Y1), .Bout(sub_2_bout));
  Sub sub_3 (.A(A0[2]), .B(A1[2]), .Bin(sub_2_bout), .Diff(Y2), .Bout(sub_3_bout));
  Sub sub_4 (.A(A0[3]), .B(A1[3]), .Bin(sub_3_bout), .Diff(Y3), .Bout(Bout));
endmodule

module ones_complement_adder_4bit (
  input  [3:0] in_1,
  input  [3:0] in_2,
  output [3:0] out_3
);

  wire not_1_out, not_2_out, not_3_out, not_4_out, not_5_out, not_6_out, not_7_out, not_8_out, not_9_out,
       sign_magnitude_adder_4bit_1_y0, sign_magnitude_adder_4bit_1_y1, sign_magnitude_adder_4bit_1_y2;
  wire [2:0] mux2to1_1_y, mux2to1_4_y;

  not not_1 (not_1_out, in_1[0]);
  not not_2 (not_2_out, in_1[1]);
  not not_3 (not_3_out, in_1[2]);
  not not_4 (not_4_out, in_2[0]);
  not not_5 (not_5_out, in_2[1]);
  not not_6 (not_6_out, in_2[2]);
  Mux2to1 mux2to1_1 (.D0(in_1[0]), .S(in_1[3]), .D1(not_1_out), .Y(mux2to1_1_y[0]));
  Mux2to1 mux2to1_2 (.D0(in_1[1]), .S(in_1[3]), .D1(not_2_out), .Y(mux2to1_1_y[1]));
  Mux2to1 mux2to1_3 (.D0(in_1[2]), .S(in_1[3]), .D1(not_3_out), .Y(mux2to1_1_y[2]));
  Mux2to1 mux2to1_4 (.D0(in_2[0]), .S(in_2[3]), .D1(not_4_out), .Y(mux2to1_4_y[0]));
  Mux2to1 mux2to1_5 (.D0(in_2[1]), .S(in_2[3]), .D1(not_5_out), .Y(mux2to1_4_y[1]));
  Mux2to1 mux2to1_6 (.D0(in_2[2]), .S(in_2[3]), .D1(not_6_out), .Y(mux2to1_4_y[2]));
  Sign_magnitude_adder_4bit sign_magnitude_adder_4bit_1 (
    .A({in_1[3], mux2to1_1_y}), .B({in_2[3], mux2to1_4_y}), .Y0(sign_magnitude_adder_4bit_1_y0),
    .Y1(sign_magnitude_adder_4bit_1_y1), .Y2(sign_magnitude_adder_4bit_1_y2), .Y3(out_3[3]));
  not not_7 (not_7_out, sign_magnitude_adder_4bit_1_y0);
  not not_8 (not_8_out, sign_magnitude_adder_4bit_1_y1);
  not not_9 (not_9_out, sign_magnitude_adder_4bit_1_y2);
  Mux2to1 mux2to1_7 (.D0(sign_magnitude_adder_4bit_1_y0), .S(out_3[3]), .D1(not_7_out), .Y(out_3[0]));
  Mux2to1 mux2to1_8 (.D0(sign_magnitude_adder_4bit_1_y1), .S(out_3[3]), .D1(not_8_out), .Y(out_3[1]));
  Mux2to1 mux2to1_9 (.D0(sign_magnitude_adder_4bit_1_y2), .S(out_3[3]), .D1(not_9_out), .Y(out_3[2]));
endmodule

module SR_Latch (
  input  R,
  input  S,
  output Q,
  output Q_n
);

  nor nor_1 (Q, R, Q_n);
  nor nor_2 (Q_n, Q, S);
endmodule

module D_Latch (
  input  WE,
  input  Reset,
  input  D,
  output Q,
  output Q_not
);

  wire and_1_out, and_2_out, and_3_out, not_1_out, not_2_out, or_1_out;

  not not_1 (not_1_out, Reset);
  and and_1 (and_1_out, not_1_out, D);
  not not_2 (not_2_out, and_1_out);
  or or_1 (or_1_out, WE, Reset);
  and and_2 (and_2_out, and_1_out, or_1_out);
  and and_3 (and_3_out, or_1_out, not_2_out);
  SR_Latch sr_latch_1 (.R(and_3_out), .S(and_2_out), .Q(Q), .Q_n(Q_not));
endmodule

module D_Flip_Flop (
  input  clock,
  input  D,
  input  EN,
  input  Reset,
  output Q,
  output Q_not
);

  wire d_latch_1_q, mux2to1_1_y, not_1_out;

  Mux2to1 mux2to1_1 (.D0(Q), .S(EN), .D1(D), .Y(mux2to1_1_y));
  not not_1 (not_1_out, clock);
  D_Latch d_latch_1 (.WE(not_1_out), .Reset(Reset), .D(mux2to1_1_y), .Q(d_latch_1_q));  // open: Q_not
  D_Latch d_latch_2 (.WE(clock), .Reset(Reset), .D(d_latch_1_q), .Q(Q), .Q_not(Q_not));
endmodule

module register_4bit (
  input  reset,
  input  EN,
  input  clock,
  input  D0,
  input  D1,
  input  D2,
  input  D3,
  output Q0,
  output Q1,
  output Q2,
  output Q3
);

  wire segment_7_0tof_1_s0, segment_7_0tof_1_s1, segment_7_0tof_1_s2, segment_7_0tof_1_s3,
       segment_7_0tof_1_x0, segment_7_0tof_1_x1, segment_7_0tof_1_x2;

  D_Flip_Flop d_flip_flop_1 (.clock(clock), .D(D0), .EN(EN), .Reset(reset), .Q(Q0));  // open: Q_not
  D_Flip_Flop d_flip_flop_2 (.clock(clock), .D(D1), .EN(EN), .Reset(reset), .Q(Q1));  // open: Q_not
  D_Flip_Flop d_flip_flop_3 (.clock(clock), .D(D2), .EN(EN), .Reset(reset), .Q(Q2));  // open: Q_not
  D_Flip_Flop d_flip_flop_4 (.clock(clock), .D(D3), .EN(EN), .Reset(reset), .Q(Q3));  // open: Q_not
  segment_7_0toF segment_7_0tof_1 (
    .A0(Q0), .A1(Q1), .A2(Q2), .A3(Q3), .S0(segment_7_0tof_1_s0), .S1(segment_7_0tof_1_s1),
    .S2(segment_7_0tof_1_s2), .S3(segment_7_0tof_1_s3), .X0(segment_7_0tof_1_x0), .X1(segment_7_0tof_1_x1),
    .X2(segment_7_0tof_1_x2));  // open: X3
  _7_Segment_Display u_7_segment_display_1 (
    .g(segment_7_0tof_1_s0), .f(segment_7_0tof_1_s1), .a(segment_7_0tof_1_s2), .b(segment_7_0tof_1_s3),
    .e(segment_7_0tof_1_x0), .d(segment_7_0tof_1_x1), .c(segment_7_0tof_1_x2));  // open: dp
endmodule

module counter_4bit (
  input  reset,
  input  enable,
  input  clock,
  input  set,
  input  set_A0,
  input  set_A1,
  input  set_A2,
  input  set_A3,
  output Y0,
  output Y1,
  output Y2,
  output Y3
);

  wire add_4bit_1_y0, add_4bit_1_y1, add_4bit_1_y2, add_4bit_1_y3, mux2to1_1_y, mux2to1_2_y, mux2to1_3_y,
       mux2to1_4_y, segment_7_0tof_1_s0, segment_7_0tof_1_s1, segment_7_0tof_1_s2, segment_7_0tof_1_s3,
       segment_7_0tof_1_x0, segment_7_0tof_1_x1, segment_7_0tof_1_x2;

  Add_4bit add_4bit_1 (
    .A0({Y3, Y2, Y1, Y0}), .A1(4'b0001), .Y0(add_4bit_1_y0), .Y1(add_4bit_1_y1), .Y2(add_4bit_1_y2),
    .Y3(add_4bit_1_y3));  // open: Cout, Overflow
  Mux2to1 mux2to1_1 (.D0(add_4bit_1_y0), .S(set), .D1(set_A0), .Y(mux2to1_1_y));
  Mux2to1 mux2to1_2 (.D0(add_4bit_1_y1), .S(set), .D1(set_A1), .Y(mux2to1_2_y));
  Mux2to1 mux2to1_3 (.D0(add_4bit_1_y2), .S(set), .D1(set_A2), .Y(mux2to1_3_y));
  Mux2to1 mux2to1_4 (.D0(add_4bit_1_y3), .S(set), .D1(set_A3), .Y(mux2to1_4_y));
  register_4bit register_4bit_1 (
    .reset(reset), .EN(enable), .clock(clock), .D0(mux2to1_1_y), .D1(mux2to1_2_y), .D2(mux2to1_3_y),
    .D3(mux2to1_4_y), .Q0(Y0), .Q1(Y1), .Q2(Y2), .Q3(Y3));
  segment_7_0toF segment_7_0tof_1 (
    .A0(Y0), .A1(Y1), .A2(Y2), .A3(Y3), .S0(segment_7_0tof_1_s0), .S1(segment_7_0tof_1_s1),
    .S2(segment_7_0tof_1_s2), .S3(segment_7_0tof_1_s3), .X0(segment_7_0tof_1_x0), .X1(segment_7_0tof_1_x1),
    .X2(segment_7_0tof_1_x2));  // open: X3
  _7_Segment_Display u_7_segment_display_1 (
    .g(segment_7_0tof_1_s0), .f(segment_7_0tof_1_s1), .a(segment_7_0tof_1_s2), .b(segment_7_0tof_1_s3),
    .e(segment_7_0tof_1_x0), .d(segment_7_0tof_1_x1), .c(segment_7_0tof_1_x2));  // open: dp
endmodule

module SequenceSummation (
  input  in_1
);

  wire add_8bit_1_y0, add_8bit_1_y1, add_8bit_1_y2, add_8bit_1_y3, add_8bit_1_y4, add_8bit_1_y5,
       add_8bit_1_y6, add_8bit_1_y7, clock_1_out, nand_1_out, not_1_out, segment_7_0tof_1_s0,
       segment_7_0tof_1_s1, segment_7_0tof_1_s2, segment_7_0tof_1_s3, segment_7_0tof_1_x0,
       segment_7_0tof_1_x1, segment_7_0tof_1_x2, segment_7_0tof_2_s0, segment_7_0tof_2_s1,
       segment_7_0tof_2_s2, segment_7_0tof_2_s3, segment_7_0tof_2_x0, segment_7_0tof_2_x1,
       segment_7_0tof_2_x2, segment_7_0tof_3_s0, segment_7_0tof_3_s1, segment_7_0tof_3_s2,
       segment_7_0tof_3_s3, segment_7_0tof_3_x0, segment_7_0tof_3_x1, segment_7_0tof_3_x2;
  wire [3:0] counter_4bit_1_y0;
  wire [7:0] register_8bit_1_q0;

  Clock clock_1 (.out(clock_1_out));
  counter_4bit counter_4bit_1 (
    .reset(in_1), .enable(nand_1_out), .clock(clock_1_out), .Y0(counter_4bit_1_y0[0]),
    .Y1(counter_4bit_1_y0[1]), .Y2(counter_4bit_1_y0[2]), .Y3(counter_4bit_1_y0[3]));  // open: set, set_A0, set_A1, set_A2, set_A3
  segment_7_0toF segment_7_0tof_1 (
    .A0(counter_4bit_1_y0[0]), .A1(counter_4bit_1_y0[1]), .A2(counter_4bit_1_y0[2]),
    .A3(counter_4bit_1_y0[3]), .S0(segment_7_0tof_1_s0), .S1(segment_7_0tof_1_s1), .S2(segment_7_0tof_1_s2),
    .S3(segment_7_0tof_1_s3), .X0(segment_7_0tof_1_x0), .X1(segment_7_0tof_1_x1), .X2(segment_7_0tof_1_x2));  // open: X3
  _7_Segment_Display u_7_segment_display_1 (
    .g(segment_7_0tof_1_s0), .f(segment_7_0tof_1_s1), .a(segment_7_0tof_1_s2), .b(segment_7_0tof_1_s3),
    .e(segment_7_0tof_1_x0), .d(segment_7_0tof_1_x1), .c(segment_7_0tof_1_x2));  // open: dp
  not not_1 (not_1_out, counter_4bit_1_y0[2]);
  Add_8bit add_8bit_1 (
    .A0(register_8bit_1_q0), .A1({4'b0000, counter_4bit_1_y0}), .Y0(add_8bit_1_y0), .Y1(add_8bit_1_y1),
    .Y2(add_8bit_1_y2), .Y3(add_8bit_1_y3), .Y4(add_8bit_1_y4), .Y5(add_8bit_1_y5), .Y6(add_8bit_1_y6),
    .Y7(add_8bit_1_y7));  // open: Cout, Overflow
  nand nand_1 (nand_1_out, counter_4bit_1_y0[3], not_1_out, counter_4bit_1_y0[1], counter_4bit_1_y0[0]);
  register_8bit register_8bit_1 (
    .reset(in_1), .EN(nand_1_out), .clock(clock_1_out), .D0(add_8bit_1_y0), .D1(add_8bit_1_y1),
    .D2(add_8bit_1_y2), .D3(add_8bit_1_y3), .D4(add_8bit_1_y4), .D5(add_8bit_1_y5), .D6(add_8bit_1_y6),
    .D7(add_8bit_1_y7), .Q0(register_8bit_1_q0[0]), .Q1(register_8bit_1_q0[1]), .Q2(register_8bit_1_q0[2]),
    .Q3(register_8bit_1_q0[3]), .Q4(register_8bit_1_q0[4]), .Q5(register_8bit_1_q0[5]),
    .Q6(register_8bit_1_q0[6]), .Q7(register_8bit_1_q0[7]));
  segment_7_0toF segment_7_0tof_2 (
    .A0(register_8bit_1_q0[0]), .A1(register_8bit_1_q0[1]), .A2(register_8bit_1_q0[2]),
    .A3(register_8bit_1_q0[3]), .S0(segment_7_0tof_2_s0), .S1(segment_7_0tof_2_s1), .S2(segment_7_0tof_2_s2),
    .S3(segment_7_0tof_2_s3), .X0(segment_7_0tof_2_x0), .X1(segment_7_0tof_2_x1), .X2(segment_7_0tof_2_x2));  // open: X3
  segment_7_0toF segment_7_0tof_3 (
    .A0(register_8bit_1_q0[4]), .A1(register_8bit_1_q0[5]), .A2(register_8bit_1_q0[6]),
    .A3(register_8bit_1_q0[7]), .S0(segment_7_0tof_3_s0), .S1(segment_7_0tof_3_s1), .S2(segment_7_0tof_3_s2),
    .S3(segment_7_0tof_3_s3), .X0(segment_7_0tof_3_x0), .X1(segment_7_0tof_3_x1), .X2(segment_7_0tof_3_x2));  // open: X3
  _7_Segment_Display u_7_segment_display_2 (
    .g(segment_7_0tof_3_s0), .f(segment_7_0tof_3_s1), .a(segment_7_0tof_3_s2), .b(segment_7_0tof_3_s3),
    .e(segment_7_0tof_3_x0), .d(segment_7_0tof_3_x1), .c(segment_7_0tof_3_x2));  // open: dp
  _7_Segment_Display u_7_segment_display_3 (
    .g(segment_7_0tof_2_s0), .f(segment_7_0tof_2_s1), .a(segment_7_0tof_2_s2), .b(segment_7_0tof_2_s3),
    .e(segment_7_0tof_2_x0), .d(segment_7_0tof_2_x1), .c(segment_7_0tof_2_x2));  // open: dp
endmodule

module Add_8bit (
  input  [7:0] A0,
  input  [7:0] A1,
  output Y0,
  output Y1,
  output Y2,
  output Y3,
  output Y4,
  output Y5,
  output Y6,
  output Y7,
  output Cout,
  output Overflow
);

  wire add_1_cout, add_2_cout, add_3_cout, add_4_cout, add_5_cout, add_6_cout, add_7_cout;

  Add add_1 (.A(A0[0]), .B(A1[0]), .Sum(Y0), .Cout(add_1_cout));  // open: Cin
  Add add_2 (.A(A0[1]), .B(A1[1]), .Cin(add_1_cout), .Sum(Y1), .Cout(add_2_cout));
  Add add_3 (.A(A0[2]), .B(A1[2]), .Cin(add_2_cout), .Sum(Y2), .Cout(add_3_cout));
  Add add_4 (.A(A0[3]), .B(A1[3]), .Cin(add_3_cout), .Sum(Y3), .Cout(add_4_cout));
  Add add_5 (.A(A0[4]), .B(A1[4]), .Cin(add_4_cout), .Sum(Y4), .Cout(add_5_cout));
  Add add_6 (.A(A0[5]), .B(A1[5]), .Cin(add_5_cout), .Sum(Y5), .Cout(add_6_cout));
  Add add_7 (.A(A0[6]), .B(A1[6]), .Cin(add_6_cout), .Sum(Y6), .Cout(add_7_cout));
  Add add_8 (.A(A0[7]), .B(A1[7]), .Cin(add_7_cout), .Sum(Y7), .Cout(Cout));
  xor xor_1 (Overflow, add_7_cout, Cout);
endmodule

module register_8bit (
  input  reset,
  input  EN,
  input  clock,
  input  D0,
  input  D1,
  input  D2,
  input  D3,
  input  D4,
  input  D5,
  input  D6,
  input  D7,
  output Q0,
  output Q1,
  output Q2,
  output Q3,
  output Q4,
  output Q5,
  output Q6,
  output Q7
);

  D_Flip_Flop d_flip_flop_1 (.clock(clock), .D(D0), .EN(EN), .Reset(reset), .Q(Q0));  // open: Q_not
  D_Flip_Flop d_flip_flop_2 (.clock(clock), .D(D4), .EN(EN), .Reset(reset), .Q(Q4));  // open: Q_not
  D_Flip_Flop d_flip_flop_3 (.clock(clock), .D(D1), .EN(EN), .Reset(reset), .Q(Q1));  // open: Q_not
  D_Flip_Flop d_flip_flop_4 (.clock(clock), .D(D5), .EN(EN), .Reset(reset), .Q(Q5));  // open: Q_not
  D_Flip_Flop d_flip_flop_5 (.clock(clock), .D(D2), .EN(EN), .Reset(reset), .Q(Q2));  // open: Q_not
  D_Flip_Flop d_flip_flop_6 (.clock(clock), .D(D6), .EN(EN), .Reset(reset), .Q(Q6));  // open: Q_not
  D_Flip_Flop d_flip_flop_7 (.clock(clock), .D(D3), .EN(EN), .Reset(reset), .Q(Q3));  // open: Q_not
  D_Flip_Flop d_flip_flop_8 (.clock(clock), .D(D7), .EN(EN), .Reset(reset), .Q(Q7));  // open: Q_not
endmodule

module clock_and_second (
  input  in_1
);

  wire and_1_out, and_2_out, clock_1_out, counter_4bit_1_y0, counter_4bit_1_y1, counter_4bit_1_y2,
       counter_4bit_1_y3, counter_8bit_1_q0, counter_8bit_1_q1, counter_8bit_1_q2, counter_8bit_1_q3,
       counter_8bit_1_q4, counter_8bit_1_q5, counter_8bit_1_q6, counter_8bit_1_q7, not_1_out, not_2_out,
       or_1_out, segment_7_0tof_1_s0, segment_7_0tof_1_s1, segment_7_0tof_1_s2, segment_7_0tof_1_s3,
       segment_7_0tof_1_x0, segment_7_0tof_1_x1, segment_7_0tof_1_x2, segment_7_0tof_2_s0,
       segment_7_0tof_2_s1, segment_7_0tof_2_s2, segment_7_0tof_2_s3, segment_7_0tof_2_x0,
       segment_7_0tof_2_x1, segment_7_0tof_2_x2, segment_7_0tof_3_s0, segment_7_0tof_3_s1,
       segment_7_0tof_3_s2, segment_7_0tof_3_s3, segment_7_0tof_3_x0, segment_7_0tof_3_x1,
       segment_7_0tof_3_x2;

  or or_1 (or_1_out, and_1_out, in_1);
  Clock clock_1 (.out(clock_1_out));
  counter_8bit counter_8bit_1 (
    .reset(or_1_out), .enable(1'b1), .clock(clock_1_out), .Q0(counter_8bit_1_q0), .Q1(counter_8bit_1_q1),
    .Q2(counter_8bit_1_q2), .Q3(counter_8bit_1_q3), .Q4(counter_8bit_1_q4), .Q5(counter_8bit_1_q5),
    .Q6(counter_8bit_1_q6), .Q7(counter_8bit_1_q7));
  not not_1 (not_1_out, counter_8bit_1_q0);
  not not_2 (not_2_out, counter_8bit_1_q1);
  and and_1 (and_1_out, not_1_out, not_2_out, counter_8bit_1_q2, counter_8bit_1_q3, counter_8bit_1_q4, counter_8bit_1_q5);
  segment_7_0toF segment_7_0tof_1 (
    .A0(counter_8bit_1_q0), .A1(counter_8bit_1_q1), .A2(counter_8bit_1_q2), .A3(counter_8bit_1_q3),
    .S0(segment_7_0tof_1_s0), .S1(segment_7_0tof_1_s1), .S2(segment_7_0tof_1_s2), .S3(segment_7_0tof_1_s3),
    .X0(segment_7_0tof_1_x0), .X1(segment_7_0tof_1_x1), .X2(segment_7_0tof_1_x2));  // open: X3
  segment_7_0toF segment_7_0tof_2 (
    .A0(counter_8bit_1_q4), .A1(counter_8bit_1_q5), .A2(counter_8bit_1_q6), .A3(counter_8bit_1_q7),
    .S0(segment_7_0tof_2_s0), .S1(segment_7_0tof_2_s1), .S2(segment_7_0tof_2_s2), .S3(segment_7_0tof_2_s3),
    .X0(segment_7_0tof_2_x0), .X1(segment_7_0tof_2_x1), .X2(segment_7_0tof_2_x2));  // open: X3
  and and_2 (and_2_out, and_1_out, clock_1_out);
  counter_4bit counter_4bit_1 (
    .reset(in_1), .enable(1'b1), .clock(and_2_out), .set(and_2_out), .set_A0(and_2_out), .set_A1(and_2_out),
    .set_A2(and_2_out), .Y0(counter_4bit_1_y0), .Y1(counter_4bit_1_y1), .Y2(counter_4bit_1_y2),
    .Y3(counter_4bit_1_y3));  // open: set_A3
  segment_7_0toF segment_7_0tof_3 (
    .A0(counter_4bit_1_y0), .A1(counter_4bit_1_y1), .A2(counter_4bit_1_y2), .A3(counter_4bit_1_y3),
    .S0(segment_7_0tof_3_s0), .S1(segment_7_0tof_3_s1), .S2(segment_7_0tof_3_s2), .S3(segment_7_0tof_3_s3),
    .X0(segment_7_0tof_3_x0), .X1(segment_7_0tof_3_x1), .X2(segment_7_0tof_3_x2));  // open: X3
  _7_Segment_Display u_7_segment_display_1 (
    .g(segment_7_0tof_3_s0), .f(segment_7_0tof_3_s1), .a(segment_7_0tof_3_s2), .b(segment_7_0tof_3_s3),
    .e(segment_7_0tof_3_x0), .d(segment_7_0tof_3_x1), .c(segment_7_0tof_3_x2));  // open: dp
  _7_Segment_Display u_7_segment_display_2 (
    .g(segment_7_0tof_2_s0), .f(segment_7_0tof_2_s1), .a(segment_7_0tof_2_s2), .b(segment_7_0tof_2_s3),
    .e(segment_7_0tof_2_x0), .d(segment_7_0tof_2_x1), .c(segment_7_0tof_2_x2));  // open: dp
  _7_Segment_Display u_7_segment_display_3 (
    .g(segment_7_0tof_1_s0), .f(segment_7_0tof_1_s1), .a(segment_7_0tof_1_s2), .b(segment_7_0tof_1_s3),
    .e(segment_7_0tof_1_x0), .d(segment_7_0tof_1_x1), .c(segment_7_0tof_1_x2));  // open: dp
endmodule

module counter_8bit (
  input  reset,
  input  enable,
  input  clock,
  output Q0,
  output Q1,
  output Q2,
  output Q3,
  output Q4,
  output Q5,
  output Q6,
  output Q7
);

  wire add_8bit_1_y0, add_8bit_1_y1, add_8bit_1_y2, add_8bit_1_y3, add_8bit_1_y4, add_8bit_1_y5,
       add_8bit_1_y6, add_8bit_1_y7;

  Add_8bit add_8bit_1 (
    .A0({Q7, Q6, Q5, Q4, Q3, Q2, Q1, Q0}), .A1(8'h1), .Y0(add_8bit_1_y0), .Y1(add_8bit_1_y1),
    .Y2(add_8bit_1_y2), .Y3(add_8bit_1_y3), .Y4(add_8bit_1_y4), .Y5(add_8bit_1_y5), .Y6(add_8bit_1_y6),
    .Y7(add_8bit_1_y7));  // open: Cout, Overflow
  register_8bit register_8bit_1 (
    .reset(reset), .EN(enable), .clock(clock), .D0(add_8bit_1_y0), .D1(add_8bit_1_y1), .D2(add_8bit_1_y2),
    .D3(add_8bit_1_y3), .D4(add_8bit_1_y4), .D5(add_8bit_1_y5), .D6(add_8bit_1_y6), .D7(add_8bit_1_y7),
    .Q0(Q0), .Q1(Q1), .Q2(Q2), .Q3(Q3), .Q4(Q4), .Q5(Q5), .Q6(Q6), .Q7(Q7));
endmodule

module ROM_8x8 (
  input  A0,
  input  A1,
  input  A2,
  output Q7,
  output Q6,
  output Q5,
  output Q4,
  output Q3,
  output Q2,
  output Q1,
  output Q0
);

  wire and_1_out, and_2_out, and_3_out, and_4_out, and_5_out, and_6_out, and_7_out, and_8_out, and_9_out,
       and_10_out, and_11_out, and_12_out, and_13_out, and_14_out, and_15_out, and_16_out, and_17_out,
       and_18_out, and_19_out, and_20_out, and_21_out, and_22_out, and_23_out, and_24_out, and_25_out,
       and_26_out, and_27_out, and_28_out, and_29_out, and_30_out, and_31_out, and_32_out, and_33_out,
       and_34_out, and_35_out, and_36_out, and_37_out, and_38_out, and_39_out, and_40_out, and_41_out,
       and_42_out, and_43_out, and_44_out, and_45_out, and_46_out, and_47_out, and_48_out, and_49_out,
       and_50_out, and_51_out, and_52_out, and_53_out, and_54_out, and_55_out, and_56_out, and_57_out,
       and_58_out, and_59_out, and_60_out, and_61_out, and_62_out, and_63_out, and_64_out, decoder3_8_1_y0,
       decoder3_8_1_y1, decoder3_8_1_y2, decoder3_8_1_y3, decoder3_8_1_y4, decoder3_8_1_y5, decoder3_8_1_y6,
       decoder3_8_1_y7, not_1_out;

  Decoder3_8 decoder3_8_1 (
    .A0(A0), .A1(A1), .A2(A2), .enable(1'b1), .Y0(decoder3_8_1_y0), .Y1(decoder3_8_1_y1),
    .Y2(decoder3_8_1_y2), .Y3(decoder3_8_1_y3), .Y4(decoder3_8_1_y4), .Y5(decoder3_8_1_y5),
    .Y6(decoder3_8_1_y6), .Y7(decoder3_8_1_y7));
  and and_1 (and_1_out, decoder3_8_1_y0, 1'b1);
  not not_1 (not_1_out, 1'b1);
  and and_2 (and_2_out, decoder3_8_1_y1, 1'b1);
  and and_3 (and_3_out, decoder3_8_1_y2, 1'b1);
  and and_4 (and_4_out, decoder3_8_1_y3, 1'b1);
  and and_5 (and_5_out, decoder3_8_1_y4, not_1_out);
  and and_6 (and_6_out, decoder3_8_1_y5, not_1_out);
  and and_7 (and_7_out, decoder3_8_1_y6, 1'b1);
  and and_8 (and_8_out, decoder3_8_1_y7, not_1_out);
  or or_1 (Q7, and_5_out, and_8_out, and_1_out, and_3_out, and_2_out, and_4_out, and_7_out, and_6_out);
  and and_9 (and_9_out, decoder3_8_1_y0, not_1_out);
  and and_10 (and_10_out, decoder3_8_1_y1, not_1_out);
  and and_11 (and_11_out, decoder3_8_1_y2, not_1_out);
  and and_12 (and_12_out, decoder3_8_1_y3, not_1_out);
  and and_13 (and_13_out, decoder3_8_1_y4, not_1_out);
  and and_14 (and_14_out, decoder3_8_1_y5, not_1_out);
  and and_15 (and_15_out, decoder3_8_1_y6, 1'b1);
  and and_16 (and_16_out, decoder3_8_1_y7, 1'b1);
  or or_2 (Q6, and_14_out, and_16_out, and_9_out, and_10_out, and_12_out, and_11_out, and_15_out, and_13_out);
  and and_17 (and_17_out, decoder3_8_1_y0, not_1_out);
  and and_18 (and_18_out, decoder3_8_1_y1, not_1_out);
  and and_19 (and_19_out, decoder3_8_1_y2, 1'b1);
  and and_20 (and_20_out, decoder3_8_1_y3, 1'b1);
  and and_21 (and_21_out, decoder3_8_1_y4, not_1_out);
  and and_22 (and_22_out, decoder3_8_1_y5, 1'b1);
  and and_23 (and_23_out, decoder3_8_1_y6, not_1_out);
  and and_24 (and_24_out, decoder3_8_1_y7, 1'b1);
  or or_3 (Q5, and_24_out, and_23_out, and_22_out, and_21_out, and_17_out, and_18_out, and_19_out, and_20_out);
  and and_25 (and_25_out, decoder3_8_1_y0, not_1_out);
  and and_26 (and_26_out, decoder3_8_1_y1, 1'b1);
  and and_27 (and_27_out, decoder3_8_1_y2, decoder3_8_1_y1);
  and and_28 (and_28_out, decoder3_8_1_y3, 1'b1);
  and and_29 (and_29_out, decoder3_8_1_y4, 1'b1);
  and and_30 (and_30_out, decoder3_8_1_y5, decoder3_8_1_y1);
  and and_31 (and_31_out, decoder3_8_1_y6, 1'b1);
  and and_32 (and_32_out, decoder3_8_1_y7, not_1_out);
  or or_4 (Q4, and_25_out, and_32_out, and_31_out, and_30_out, and_29_out, and_27_out, and_26_out, and_28_out);
  and and_33 (and_33_out, decoder3_8_1_y0, 1'b1);
  and and_34 (and_34_out, decoder3_8_1_y1, not_1_out);
  and and_35 (and_35_out, decoder3_8_1_y2, not_1_out);
  and and_36 (and_36_out, decoder3_8_1_y3, not_1_out);
  and and_37 (and_37_out, decoder3_8_1_y4, not_1_out);
  and and_38 (and_38_out, decoder3_8_1_y5, 1'b1);
  and and_39 (and_39_out, decoder3_8_1_y6, not_1_out);
  and and_40 (and_40_out, decoder3_8_1_y7, 1'b1);
  or or_5 (Q3, and_33_out, and_40_out, and_34_out, and_39_out, and_35_out, and_38_out, and_37_out, and_36_out);
  and and_41 (and_41_out, decoder3_8_1_y0, not_1_out);
  and and_42 (and_42_out, decoder3_8_1_y1, not_1_out);
  and and_43 (and_43_out, decoder3_8_1_y2, not_1_out);
  and and_44 (and_44_out, decoder3_8_1_y3, not_1_out);
  and and_45 (and_45_out, decoder3_8_1_y4, 1'b1);
  and and_46 (and_46_out, decoder3_8_1_y5, not_1_out);
  and and_47 (and_47_out, decoder3_8_1_y6, not_1_out);
  and and_48 (and_48_out, decoder3_8_1_y7, 1'b1);
  or or_6 (Q2, and_48_out, and_47_out, and_46_out, and_45_out, and_41_out, and_44_out, and_43_out, and_42_out);
  and and_49 (and_49_out, decoder3_8_1_y0, not_1_out);
  and and_50 (and_50_out, decoder3_8_1_y1, not_1_out);
  and and_51 (and_51_out, decoder3_8_1_y2, not_1_out);
  and and_52 (and_52_out, decoder3_8_1_y3, 1'b1);
  and and_53 (and_53_out, decoder3_8_1_y4, 1'b1);
  and and_54 (and_54_out, decoder3_8_1_y5, not_1_out);
  and and_55 (and_55_out, decoder3_8_1_y6, not_1_out);
  and and_56 (and_56_out, decoder3_8_1_y7, 1'b1);
  or or_7 (Q1, and_56_out, and_55_out, and_54_out, and_53_out, and_52_out, and_51_out, and_50_out, and_49_out);
  and and_57 (and_57_out, decoder3_8_1_y0, 1'b1);
  and and_58 (and_58_out, decoder3_8_1_y1, 1'b1);
  and and_59 (and_59_out, decoder3_8_1_y2, 1'b1);
  and and_60 (and_60_out, decoder3_8_1_y3, not_1_out);
  and and_61 (and_61_out, decoder3_8_1_y4, 1'b1);
  and and_62 (and_62_out, decoder3_8_1_y5, 1'b1);
  and and_63 (and_63_out, decoder3_8_1_y6, 1'b1);
  and and_64 (and_64_out, decoder3_8_1_y7, 1'b1);
  or or_8 (Q0, and_64_out, and_63_out, and_62_out, and_61_out, and_60_out, and_59_out, and_58_out, and_57_out);
endmodule

module RAM_4x8 (
  input  A0,
  input  A1,
  input  A2,
  input  reset,
  input  enable,
  input  clock,
  input  D0,
  input  D1,
  input  D2,
  input  D3,
  input  D4,
  input  D5,
  input  D6,
  input  D7,
  input  B0,
  input  B1,
  input  B2,
  output Q0,
  output Q1,
  output Q2,
  output Q3,
  output Q4,
  output Q5,
  output Q6,
  output Q7,
  output Y0,
  output Y1,
  output Y2,
  output Y3,
  output Y4,
  output Y5,
  output Y6,
  output Y7
);

  wire and_1_out, and_2_out, and_3_out, and_4_out;
  wire [7:0] and_5_out, and_6_out, and_7_out, and_8_out, and_9_out, and_10_out, and_11_out, and_12_out,
       register_8bit_1_q0, register_8bit_2_q0, register_8bit_3_q0, register_8bit_4_q0;
  wire [7:7] decoder3_8_1_y0, decoder3_8_1_y1, decoder3_8_1_y2, decoder3_8_1_y3, decoder3_8_2_y0,
       decoder3_8_2_y1, decoder3_8_2_y2, decoder3_8_2_y3;

  Decoder3_8 decoder3_8_1 (
    .A0(B0), .A1(B1), .A2(B2), .enable(1'b1), .Y0(decoder3_8_1_y0[7]), .Y1(decoder3_8_1_y1[7]),
    .Y2(decoder3_8_1_y2[7]), .Y3(decoder3_8_1_y3[7]));  // open: Y4, Y5, Y6, Y7
  Decoder3_8 decoder3_8_2 (
    .A0(A0), .A1(A1), .A2(A2), .enable(1'b1), .Y0(decoder3_8_2_y0[7]), .Y1(decoder3_8_2_y1[7]),
    .Y2(decoder3_8_2_y2[7]), .Y3(decoder3_8_2_y3[7]));  // open: Y4, Y5, Y6, Y7
  and and_1 (and_1_out, decoder3_8_2_y0[7], enable);
  and and_2 (and_2_out, decoder3_8_2_y1[7], enable);
  and and_3 (and_3_out, enable, decoder3_8_2_y2[7]);
  and and_4 (and_4_out, enable, decoder3_8_2_y3[7]);
  register_8bit register_8bit_1 (
    .reset(reset), .EN(and_1_out), .clock(clock), .D0(D0), .D1(D1), .D2(D2), .D3(D3), .D4(D4), .D5(D5),
    .D6(D6), .D7(D7), .Q0(register_8bit_1_q0[0]), .Q1(register_8bit_1_q0[1]), .Q2(register_8bit_1_q0[2]),
    .Q3(register_8bit_1_q0[3]), .Q4(register_8bit_1_q0[4]), .Q5(register_8bit_1_q0[5]),
    .Q6(register_8bit_1_q0[6]), .Q7(register_8bit_1_q0[7]));
  register_8bit register_8bit_2 (
    .reset(reset), .EN(and_2_out), .clock(clock), .D0(D0), .D1(D1), .D2(D2), .D3(D3), .D4(D4), .D5(D5),
    .D6(D6), .D7(D7), .Q0(register_8bit_2_q0[0]), .Q1(register_8bit_2_q0[1]), .Q2(register_8bit_2_q0[2]),
    .Q3(register_8bit_2_q0[3]), .Q4(register_8bit_2_q0[4]), .Q5(register_8bit_2_q0[5]),
    .Q6(register_8bit_2_q0[6]), .Q7(register_8bit_2_q0[7]));
  register_8bit register_8bit_3 (
    .reset(reset), .EN(and_3_out), .clock(clock), .D0(D0), .D1(D1), .D2(D2), .D3(D3), .D4(D4), .D5(D5),
    .D6(D6), .D7(D7), .Q0(register_8bit_3_q0[0]), .Q1(register_8bit_3_q0[1]), .Q2(register_8bit_3_q0[2]),
    .Q3(register_8bit_3_q0[3]), .Q4(register_8bit_3_q0[4]), .Q5(register_8bit_3_q0[5]),
    .Q6(register_8bit_3_q0[6]), .Q7(register_8bit_3_q0[7]));
  register_8bit register_8bit_4 (
    .reset(reset), .EN(and_4_out), .clock(clock), .D0(D0), .D1(D1), .D2(D2), .D3(D3), .D4(D4), .D5(D5),
    .D6(D6), .D7(D7), .Q0(register_8bit_4_q0[0]), .Q1(register_8bit_4_q0[1]), .Q2(register_8bit_4_q0[2]),
    .Q3(register_8bit_4_q0[3]), .Q4(register_8bit_4_q0[4]), .Q5(register_8bit_4_q0[5]),
    .Q6(register_8bit_4_q0[6]), .Q7(register_8bit_4_q0[7]));
  assign and_5_out = {8{decoder3_8_1_y0[7]}} & register_8bit_1_q0;  // AND_Gate and_5, 8 bits wide
  assign and_6_out = {8{decoder3_8_1_y1[7]}} & register_8bit_2_q0;  // AND_Gate and_6, 8 bits wide
  assign and_7_out = {8{decoder3_8_1_y2[7]}} & register_8bit_3_q0;  // AND_Gate and_7, 8 bits wide
  assign and_8_out = {8{decoder3_8_1_y3[7]}} & register_8bit_4_q0;  // AND_Gate and_8, 8 bits wide
  assign and_9_out = {8{decoder3_8_2_y0[7]}} & register_8bit_1_q0;  // AND_Gate and_9, 8 bits wide
  assign and_10_out = {8{decoder3_8_2_y1[7]}} & register_8bit_2_q0;  // AND_Gate and_10, 8 bits wide
  assign and_11_out = {8{decoder3_8_2_y2[7]}} & register_8bit_3_q0;  // AND_Gate and_11, 8 bits wide
  assign and_12_out = {8{decoder3_8_2_y3[7]}} & register_8bit_4_q0;  // AND_Gate and_12, 8 bits wide
  or or_1 (Q0, and_9_out[0], and_10_out[0], and_11_out[0], and_12_out[0]);
  or or_2 (Q1, and_9_out[1], and_10_out[1], and_11_out[1], and_12_out[1]);
  or or_3 (Q2, and_9_out[2], and_10_out[2], and_11_out[2], and_12_out[2]);
  or or_4 (Q3, and_9_out[3], and_10_out[3], and_11_out[3], and_12_out[3]);
  or or_5 (Q4, and_9_out[4], and_10_out[4], and_12_out[4], and_11_out[4]);
  or or_6 (Q5, and_9_out[5], and_10_out[5], and_11_out[5], and_12_out[5]);
  or or_7 (Q6, and_9_out[6], and_10_out[6], and_11_out[6], and_12_out[6]);
  or or_8 (Q7, and_9_out[7], and_10_out[7], and_11_out[7], and_12_out[7]);
  or or_9 (Y1, and_5_out[1], and_8_out[1], and_6_out[1], and_7_out[1]);
  or or_10 (Y2, and_5_out[2], and_6_out[2], and_7_out[2], and_8_out[2]);
  or or_11 (Y3, and_5_out[3], and_6_out[3], and_7_out[3], and_8_out[3]);
  or or_12 (Y4, and_5_out[4], and_6_out[4], and_7_out[4], and_8_out[4]);
  or or_13 (Y5, and_5_out[5], and_6_out[5], and_7_out[5], and_8_out[5]);
  or or_14 (Y6, and_5_out[6], and_6_out[6], and_7_out[6], and_8_out[6]);
  or or_15 (Y7, and_6_out[7], and_5_out[7], and_7_out[7], and_8_out[7]);
  or or_16 (Y0, and_5_out[0], and_6_out[0], and_8_out[0], and_7_out[0]);
endmodule

module sCPU (
  input  in_1
);

  wire add_8bit_1_y0, add_8bit_1_y1, add_8bit_1_y2, add_8bit_1_y3, add_8bit_1_y4, add_8bit_1_y5,
       add_8bit_1_y6, add_8bit_1_y7, and_1_out, and_2_out, and_3_out, and_4_out, and_5_out, and_6_out,
       and_7_out, and_8_out, and_9_out, clock_1_out, comparator_4bit_1_same, counter_4bit_1_y0,
       counter_4bit_1_y1, counter_4bit_1_y2, decoder2_4_1_y0, decoder2_4_1_y2, decoder2_4_1_y3, mux2to1_1_y,
       mux2to1_2_y, mux2to1_3_y, mux2to1_4_y, mux2to1_5_y, mux2to1_6_y, mux2to1_7_y, mux2to1_8_y, not_1_out,
       not_2_out, or_1_out, or_2_out, or_3_out, or_4_out, rom_8x8_1_q0, rom_8x8_1_q1, rom_8x8_1_q2,
       rom_8x8_1_q3, rom_8x8_1_q4, rom_8x8_1_q5, rom_8x8_1_q6, rom_8x8_1_q7;
  wire [3:0] ram_4x8_1_y0;
  wire [7:0] and_10_out, ram_4x8_1_q4;
  wire [7:4] ram_4x8_1_y4;
  wire [7:7] decoder2_4_1_y1;

  Clock clock_1 (.out(clock_1_out));
  not not_1 (not_1_out, decoder2_4_1_y1[7]);
  and and_1 (and_1_out, decoder2_4_1_y3, not_2_out);
  counter_4bit counter_4bit_1 (
    .reset(in_1), .enable(not_1_out), .clock(clock_1_out), .set(and_1_out), .set_A0(rom_8x8_1_q2),
    .set_A1(rom_8x8_1_q3), .set_A2(rom_8x8_1_q4), .set_A3(rom_8x8_1_q5), .Y0(counter_4bit_1_y0),
    .Y1(counter_4bit_1_y1), .Y2(counter_4bit_1_y2));  // open: Y3
  not not_2 (not_2_out, comparator_4bit_1_same);
  ROM_8x8 rom_8x8_1 (
    .A0(counter_4bit_1_y0), .A1(counter_4bit_1_y1), .A2(counter_4bit_1_y2), .Q7(rom_8x8_1_q7),
    .Q6(rom_8x8_1_q6), .Q5(rom_8x8_1_q5), .Q4(rom_8x8_1_q4), .Q3(rom_8x8_1_q3), .Q2(rom_8x8_1_q2),
    .Q1(rom_8x8_1_q1), .Q0(rom_8x8_1_q0));
  Decoder2_4 decoder2_4_1 (
    .A0(rom_8x8_1_q6), .A1(rom_8x8_1_q7), .enable(1'b1), .Y0(decoder2_4_1_y0), .Y1(decoder2_4_1_y1[7]),
    .Y2(decoder2_4_1_y2), .Y3(decoder2_4_1_y3));
  or or_1 (or_1_out, decoder2_4_1_y0, decoder2_4_1_y2);
  and and_2 (and_2_out, rom_8x8_1_q4, decoder2_4_1_y1[7]);
  and and_3 (and_3_out, rom_8x8_1_q2, decoder2_4_1_y0);
  and and_4 (and_4_out, decoder2_4_1_y2, rom_8x8_1_q4);
  and and_5 (and_5_out, decoder2_4_1_y0, rom_8x8_1_q3);
  and and_6 (and_6_out, decoder2_4_1_y2, rom_8x8_1_q5);
  and and_7 (and_7_out, rom_8x8_1_q5, decoder2_4_1_y1[7]);
  or or_2 (or_2_out, decoder2_4_1_y0, decoder2_4_1_y3);
  or or_3 (or_3_out, and_3_out, and_2_out, and_4_out);
  or or_4 (or_4_out, and_5_out, and_7_out, and_6_out);
  and and_8 (and_8_out, or_2_out, rom_8x8_1_q0);
  and and_9 (and_9_out, or_2_out, rom_8x8_1_q1);
  Mux2to1 mux2to1_1 (.D0(rom_8x8_1_q0), .S(decoder2_4_1_y0), .D1(add_8bit_1_y0), .Y(mux2to1_1_y));
  Mux2to1 mux2to1_2 (.D0(rom_8x8_1_q1), .S(decoder2_4_1_y0), .D1(add_8bit_1_y1), .Y(mux2to1_2_y));
  Mux2to1 mux2to1_3 (.D0(rom_8x8_1_q2), .S(decoder2_4_1_y0), .D1(add_8bit_1_y2), .Y(mux2to1_3_y));
  Mux2to1 mux2to1_4 (.D0(rom_8x8_1_q3), .S(decoder2_4_1_y0), .D1(add_8bit_1_y3), .Y(mux2to1_4_y));
  Mux2to1 mux2to1_5 (.D0(1'b0), .S(decoder2_4_1_y0), .D1(add_8bit_1_y4), .Y(mux2to1_5_y));
  Mux2to1 mux2to1_6 (.D0(1'b0), .S(decoder2_4_1_y0), .D1(add_8bit_1_y5), .Y(mux2to1_6_y));
  Mux2to1 mux2to1_7 (.D0(1'b0), .S(decoder2_4_1_y0), .D1(add_8bit_1_y6), .Y(mux2to1_7_y));
  Mux2to1 mux2to1_8 (.D0(1'b0), .S(decoder2_4_1_y0), .D1(add_8bit_1_y7), .Y(mux2to1_8_y));
  RAM_4x8 ram_4x8_1 (
    .A0(or_3_out), .A1(or_4_out), .A2(1'b0), .reset(in_1), .enable(or_1_out), .clock(clock_1_out),
    .D0(mux2to1_1_y), .D1(mux2to1_2_y), .D2(mux2to1_3_y), .D3(mux2to1_4_y), .D4(mux2to1_5_y),
    .D5(mux2to1_6_y), .D6(mux2to1_7_y), .D7(mux2to1_8_y), .B0(and_8_out), .B1(and_9_out), .B2(1'b0),
    .Q0(ram_4x8_1_q4[0]), .Q1(ram_4x8_1_q4[1]), .Q2(ram_4x8_1_q4[2]), .Q3(ram_4x8_1_q4[3]),
    .Q4(ram_4x8_1_q4[4]), .Q5(ram_4x8_1_q4[5]), .Q6(ram_4x8_1_q4[6]), .Q7(ram_4x8_1_q4[7]),
    .Y0(ram_4x8_1_y0[0]), .Y1(ram_4x8_1_y0[1]), .Y2(ram_4x8_1_y0[2]), .Y3(ram_4x8_1_y0[3]),
    .Y4(ram_4x8_1_y4[4]), .Y5(ram_4x8_1_y4[5]), .Y6(ram_4x8_1_y4[6]), .Y7(ram_4x8_1_y4[7]));
  comparator_4bit comparator_4bit_1 (.A(ram_4x8_1_q4[3:0]), .B(ram_4x8_1_y0), .same(comparator_4bit_1_same));
  assign and_10_out = {8{decoder2_4_1_y1[7]}} & ram_4x8_1_q4;  // AND_Gate and_10, 8 bits wide
  Hex_Digit_Display hex_digit_display_1 (.value(and_10_out[7:4]));  // open: dp
  Add_8bit add_8bit_1 (
    .A0(ram_4x8_1_q4), .A1({ram_4x8_1_y4, ram_4x8_1_y0}), .Y0(add_8bit_1_y0), .Y1(add_8bit_1_y1),
    .Y2(add_8bit_1_y2), .Y3(add_8bit_1_y3), .Y4(add_8bit_1_y4), .Y5(add_8bit_1_y5), .Y6(add_8bit_1_y6),
    .Y7(add_8bit_1_y7));  // open: Cout, Overflow
  Hex_Digit_Display hex_digit_display_2 (.value(and_10_out[3:0]));  // open: dp
endmodule

module minirv (
  input  reset
);

  wire clock_1_out, logic_1_is_sb, logic_1_set, logic_1_wenable, logic_1_write, rgb_video_1_p3, VGA_body_mem;
  wire [4:0] decode_body_rd, decode_body_rs1, decode_body_rs2;
  wire [7:0] coordinates_body_x, coordinates_body_y;
  wire [11:0] decode_body_i_type_imm, decode_body_s_type_imm;
  wire [19:0] decode_body_u_type_imm;
  wire [23:0] rgb_video_1_p6;
  wire [31:0] decode_body_add, decode_body_addi, decode_body_jalr, decode_body_lbu, decode_body_lui,
       decode_body_lw, decode_body_sb, decode_body_sw, GPR_body_out1, GPR_body_out2, logic_1_memory_addr,
       logic_1_mwrite_data, logic_1_out_data, logic_1_set_data, pc_body_y0, R_A_M_body_mread_data,
       R_O_M_body_instruction;

  Clock clock_1 (.out(clock_1_out));
  pc pc_body (
    .reset(reset), .enable(1'b1), .clock(clock_1_out), .set(logic_1_set), .set_A0(logic_1_set_data),
    .Y0(pc_body_y0));
  R_O_M R_O_M_body (.pc(pc_body_y0), .instruction(R_O_M_body_instruction));
  decode decode_body (
    .instruction(R_O_M_body_instruction), .rs1(decode_body_rs1), .rs2(decode_body_rs2), .rd(decode_body_rd),
    .addi(decode_body_addi), .jalr(decode_body_jalr), .lui(decode_body_lui), .add(decode_body_add),
    .lw(decode_body_lw), .lbu(decode_body_lbu), .sw(decode_body_sw), .sb(decode_body_sb),
    .I_type_imm(decode_body_i_type_imm), .U_type_imm(decode_body_u_type_imm),
    .S_type_imm(decode_body_s_type_imm));
  coordinates coordinates_body (.addr(logic_1_memory_addr), .y(coordinates_body_y), .x(coordinates_body_x));
  // RGB_Video #(.cursor("No Cursor"), .height(256), .width(256)) rgb_video_1: pin names not known; wires that end beside it: reset, clock_1_out, rgb_video_1_p3, coordinates_body_x, coordinates_body_y, rgb_video_1_p6
  \logic  logic_1 (
    .pc(pc_body_y0), .S_type_imm(decode_body_s_type_imm), .U_type_imm(decode_body_u_type_imm),
    .I_type_imm(decode_body_i_type_imm), .rs1_data(GPR_body_out1), .rs2_data(GPR_body_out2),
    .addi(decode_body_addi), .jalr(decode_body_jalr), .lui(decode_body_lui), .add(decode_body_add),
    .lw(decode_body_lw), .mread_data(R_A_M_body_mread_data), .sw(decode_body_sw), .lbu(decode_body_lbu),
    .sb(decode_body_sb), .out_data(logic_1_out_data), .set(logic_1_set), .set_data(logic_1_set_data),
    .memory_addr(logic_1_memory_addr), .write(logic_1_write), .mwrite_data(logic_1_mwrite_data),
    .vga_data(rgb_video_1_p6), .is_sb(logic_1_is_sb), .wenable(logic_1_wenable));
  GPR GPR_body (
    .clk(clock_1_out), .wdata(logic_1_out_data), .waddr(decode_body_rd), .read1(decode_body_rs1),
    .read2(decode_body_rs2), .wenable(logic_1_wenable), .out1(GPR_body_out1), .out2(GPR_body_out2));
  is_VGA VGA_body (.addr(logic_1_memory_addr), .vga(rgb_video_1_p3), .mem(VGA_body_mem));
  R_A_M R_A_M_body (
    .memory_addr(logic_1_memory_addr), .write(logic_1_write), .clock(clock_1_out),
    .mwrite_data(logic_1_mwrite_data), .is_sb(logic_1_is_sb), .mem(VGA_body_mem),
    .mread_data(R_A_M_body_mread_data));
endmodule

module pc (
  input  reset,
  input  enable,
  input  clock,
  input  set,
  input  [31:0] set_A0,
  output [31:0] Y0
);

  wire [31:0] adder_1_out, multiplexer_1_out;

  Adder #(.width(32)) adder_1 (.a(Y0), .b(32'h4), .out(adder_1_out));  // open: cin, cout
  Multiplexer #(.width(32)) multiplexer_1 (.in0(adder_1_out), .in1(set_A0), .out(multiplexer_1_out), .sel(set));
  Register #(.width(32)) register_1 (.D(multiplexer_1_out), .en(enable), .clk(clock), .Q(Y0), .clr(reset));
endmodule

module is_addi (
  input  [6:0] opcode,
  input  [2:0] funct3,
  output [31:0] same
);

  wire [2:0] not_3_out, xor_2_out;
  wire [6:0] not_2_out, xor_1_out;
  wire [6:6] not_1_out;

  not not_1 (not_1_out[6], 1'b1);
  assign xor_1_out = {{2{not_1_out[6]}}, 1'b1, {2{not_1_out[6]}}, 2'b11} ^ opcode;  // XOR_Gate xor_1, 7 bits wide
  assign xor_2_out = funct3 ^ {3{not_1_out[6]}};  // XOR_Gate xor_2, 3 bits wide
  assign not_2_out = ~xor_1_out;  // NOT_Gate not_2, 7 bits wide
  assign not_3_out = ~xor_2_out;  // NOT_Gate not_3, 3 bits wide
  and and_1 (same[31], not_2_out[0], not_2_out[1], not_2_out[2], not_2_out[3], not_2_out[4], not_2_out[5], not_2_out[6], not_3_out[0], not_3_out[1], not_3_out[2]);

  assign same[30:0] = {31{same[31]}};
endmodule

module is_jalr (
  input  [6:0] opcode,
  input  [2:0] funct3,
  output [31:0] same
);

  wire [2:0] not_3_out, xor_2_out;
  wire [4:4] not_1_out;
  wire [6:0] not_2_out, xor_1_out;

  not not_1 (not_1_out[4], 1'b1);
  assign xor_1_out = {2'b11, {2{not_1_out[4]}}, 3'b111} ^ opcode;  // XOR_Gate xor_1, 7 bits wide
  assign xor_2_out = funct3 ^ {3{not_1_out[4]}};  // XOR_Gate xor_2, 3 bits wide
  assign not_2_out = ~xor_1_out;  // NOT_Gate not_2, 7 bits wide
  assign not_3_out = ~xor_2_out;  // NOT_Gate not_3, 3 bits wide
  and and_1 (same[31], not_2_out[0], not_2_out[1], not_2_out[2], not_2_out[3], not_2_out[4], not_2_out[5], not_2_out[6], not_3_out[0], not_3_out[1], not_3_out[2]);

  assign same[30:0] = {31{same[31]}};
endmodule

module GPR (
  input  clk,
  input  [31:0] wdata,
  input  [4:0] waddr,
  input  [4:0] read1,
  input  [4:0] read2,
  input  wenable,
  output [31:0] out1,
  output [31:0] out2
);

  wire and_1_out, and_2_out, decoder_1_out1, decoder_1_out2, decoder_1_out3, decoder_1_out4, decoder_1_out5,
       decoder_1_out6, decoder_1_out7, decoder_1_out8, decoder_1_out9, decoder_1_out10, decoder_1_out11,
       decoder_1_out12, decoder_1_out13, decoder_1_out14, decoder_1_out15, decoder_2_out0, decoder_2_out1,
       decoder_2_out2, decoder_2_out3, decoder_2_out4, decoder_2_out5, decoder_2_out6, decoder_2_out7,
       decoder_2_out8, decoder_2_out9, decoder_2_out10, decoder_2_out11, decoder_2_out12, decoder_2_out13,
       decoder_2_out14, decoder_2_out15, not_1_out, not_2_out, not_3_out;
  wire [31:0] multiplexer_1_out, multiplexer_2_out, multiplexer_3_out, multiplexer_4_out, register_1_q,
       register_2_q, register_3_q, register_4_q, register_5_q, register_6_q, register_7_q, register_8_q,
       register_9_q, register_10_q, register_11_q, register_12_q, register_13_q, register_14_q,
       register_15_q, register_16_q, register_17_q, register_18_q, register_19_q, register_20_q,
       register_21_q, register_22_q, register_23_q, register_24_q, register_25_q, register_26_q,
       register_27_q, register_28_q, register_29_q, register_30_q, register_31_q, register_32_q;

  not not_1 (not_1_out, waddr[4]);
  and and_1 (and_1_out, waddr[4], wenable);
  and and_2 (and_2_out, not_1_out, wenable);
  Decoder #(.select(4)) decoder_1 (
    .out1(decoder_1_out1), .out2(decoder_1_out2), .out3(decoder_1_out3), .out4(decoder_1_out4),
    .out5(decoder_1_out5), .out6(decoder_1_out6), .out7(decoder_1_out7), .out8(decoder_1_out8),
    .out9(decoder_1_out9), .out10(decoder_1_out10), .out11(decoder_1_out11), .out12(decoder_1_out12),
    .out13(decoder_1_out13), .out14(decoder_1_out14), .out15(decoder_1_out15), .sel(waddr[3:0]),
    .en(and_2_out));  // open: out0
  Decoder #(.select(4)) decoder_2 (
    .out0(decoder_2_out0), .out1(decoder_2_out1), .out2(decoder_2_out2), .out3(decoder_2_out3),
    .out4(decoder_2_out4), .out5(decoder_2_out5), .out6(decoder_2_out6), .out7(decoder_2_out7),
    .out8(decoder_2_out8), .out9(decoder_2_out9), .out10(decoder_2_out10), .out11(decoder_2_out11),
    .out12(decoder_2_out12), .out13(decoder_2_out13), .out14(decoder_2_out14), .out15(decoder_2_out15),
    .sel(waddr[3:0]), .en(and_1_out));
  Register #(.width(32)) register_1 (.D(wdata), .clk(clk), .Q(register_1_q), .clr(1'b1));  // open: en
  Register #(.width(32)) register_2 (.D(wdata), .en(decoder_1_out8), .clk(clk), .Q(register_2_q));  // open: clr
  Register #(.width(32)) register_3 (.D(wdata), .en(decoder_2_out0), .clk(clk), .Q(register_3_q));  // open: clr
  Register #(.width(32)) register_4 (.D(wdata), .en(decoder_2_out8), .clk(clk), .Q(register_4_q));  // open: clr
  Register #(.width(32)) register_5 (.D(wdata), .en(decoder_1_out1), .clk(clk), .Q(register_5_q));  // open: clr
  Register #(.width(32)) register_6 (.D(wdata), .en(decoder_1_out9), .clk(clk), .Q(register_6_q));  // open: clr
  Register #(.width(32)) register_7 (.D(wdata), .en(decoder_2_out1), .clk(clk), .Q(register_7_q));  // open: clr
  Register #(.width(32)) register_8 (.D(wdata), .en(decoder_2_out9), .clk(clk), .Q(register_8_q));  // open: clr
  Register #(.width(32)) register_9 (.D(wdata), .en(decoder_1_out2), .clk(clk), .Q(register_9_q));  // open: clr
  Register #(.width(32)) register_10 (.D(wdata), .en(decoder_1_out10), .clk(clk), .Q(register_10_q));  // open: clr
  Register #(.width(32)) register_11 (.D(wdata), .en(decoder_2_out2), .clk(clk), .Q(register_11_q));  // open: clr
  Register #(.width(32)) register_12 (.D(wdata), .en(decoder_2_out10), .clk(clk), .Q(register_12_q));  // open: clr
  Register #(.width(32)) register_13 (.D(wdata), .en(decoder_1_out3), .clk(clk), .Q(register_13_q));  // open: clr
  Register #(.width(32)) register_14 (.D(wdata), .en(decoder_1_out11), .clk(clk), .Q(register_14_q));  // open: clr
  Register #(.width(32)) register_15 (.D(wdata), .en(decoder_2_out3), .clk(clk), .Q(register_15_q));  // open: clr
  Register #(.width(32)) register_16 (.D(wdata), .en(decoder_2_out11), .clk(clk), .Q(register_16_q));  // open: clr
  Register #(.width(32)) register_17 (.D(wdata), .en(decoder_1_out4), .clk(clk), .Q(register_17_q));  // open: clr
  Register #(.width(32)) register_18 (.D(wdata), .en(decoder_1_out12), .clk(clk), .Q(register_18_q));  // open: clr
  Register #(.width(32)) register_19 (.D(wdata), .en(decoder_2_out4), .clk(clk), .Q(register_19_q));  // open: clr
  Register #(.width(32)) register_20 (.D(wdata), .en(decoder_2_out12), .clk(clk), .Q(register_20_q));  // open: clr
  Register #(.width(32)) register_21 (.D(wdata), .en(decoder_1_out5), .clk(clk), .Q(register_21_q));  // open: clr
  Register #(.width(32)) register_22 (.D(wdata), .en(decoder_1_out13), .clk(clk), .Q(register_22_q));  // open: clr
  Register #(.width(32)) register_23 (.D(wdata), .en(decoder_2_out5), .clk(clk), .Q(register_23_q));  // open: clr
  Register #(.width(32)) register_24 (.D(wdata), .en(decoder_2_out13), .clk(clk), .Q(register_24_q));  // open: clr
  Register #(.width(32)) register_25 (.D(wdata), .en(decoder_1_out6), .clk(clk), .Q(register_25_q));  // open: clr
  Register #(.width(32)) register_26 (.D(wdata), .en(decoder_1_out14), .clk(clk), .Q(register_26_q));  // open: clr
  Register #(.width(32)) register_27 (.D(wdata), .en(decoder_2_out6), .clk(clk), .Q(register_27_q));  // open: clr
  Register #(.width(32)) register_28 (.D(wdata), .en(decoder_2_out14), .clk(clk), .Q(register_28_q));  // open: clr
  Register #(.width(32)) register_29 (.D(wdata), .en(decoder_1_out7), .clk(clk), .Q(register_29_q));  // open: clr
  Register #(.width(32)) register_30 (.D(wdata), .en(decoder_1_out15), .clk(clk), .Q(register_30_q));  // open: clr
  Register #(.width(32)) register_31 (.D(wdata), .en(decoder_2_out7), .clk(clk), .Q(register_31_q));  // open: clr
  Register #(.width(32)) register_32 (.D(wdata), .en(decoder_2_out15), .clk(clk), .Q(register_32_q));  // open: clr
  Multiplexer #(.enable("true"), .select(4), .width(32)) multiplexer_1 (
    .in0(register_1_q), .in1(register_5_q), .in2(register_9_q), .in3(register_13_q), .in4(register_17_q),
    .in5(register_21_q), .in6(register_25_q), .in7(register_29_q), .in8(register_2_q), .in9(register_6_q),
    .in10(register_10_q), .in11(register_14_q), .in12(register_18_q), .in13(register_22_q),
    .in14(register_26_q), .in15(register_30_q), .out(multiplexer_1_out), .sel(read1[3:0]), .en(not_3_out));
  Multiplexer #(.enable("true"), .select(4), .width(32)) multiplexer_2 (
    .in0(register_1_q), .in1(register_5_q), .in2(register_9_q), .in3(register_13_q), .in4(register_17_q),
    .in5(register_21_q), .in6(register_25_q), .in7(register_29_q), .in8(register_2_q), .in9(register_6_q),
    .in10(register_10_q), .in11(register_14_q), .in12(register_18_q), .in13(register_22_q),
    .in14(register_26_q), .in15(register_30_q), .out(multiplexer_2_out), .sel(read2[3:0]), .en(not_2_out));
  Multiplexer #(.enable("true"), .select(4), .width(32)) multiplexer_3 (
    .in0(register_7_q), .in1(register_11_q), .in2(register_15_q), .in3(register_19_q), .in4(register_23_q),
    .in5(register_27_q), .in6(register_31_q), .in7(register_4_q), .in8(register_8_q), .in9(register_12_q),
    .in10(register_16_q), .in11(register_20_q), .in12(register_24_q), .in13(register_28_q),
    .in15(register_32_q), .out(multiplexer_3_out), .sel(read1[3:0]), .en(read1[4]));  // open: in14
  Multiplexer #(.enable("true"), .select(4), .width(32)) multiplexer_4 (
    .in0(register_3_q), .in1(register_7_q), .in2(register_11_q), .in3(register_15_q), .in4(register_19_q),
    .in5(register_23_q), .in6(register_27_q), .in7(register_31_q), .in8(register_4_q), .in9(register_8_q),
    .in10(register_12_q), .in11(register_16_q), .in12(register_20_q), .in13(register_24_q),
    .in14(register_28_q), .in15(register_32_q), .out(multiplexer_4_out), .sel(read2[3:0]), .en(read2[4]));
  not not_2 (not_2_out, read2[4]);
  not not_3 (not_3_out, read1[4]);
  assign out1 = multiplexer_1_out | multiplexer_3_out;  // OR_Gate or_1, 32 bits wide
  assign out2 = multiplexer_2_out | multiplexer_4_out;  // OR_Gate or_2, 32 bits wide
endmodule

module is_lui (
  input  [6:0] opcode,
  output [31:0] same
);

  wire [6:0] not_2_out, xor_1_out;
  wire [6:6] not_1_out;

  not not_1 (not_1_out[6], 1'b1);
  assign xor_1_out = {not_1_out[6], 2'b11, not_1_out[6], 3'b111} ^ opcode;  // XOR_Gate xor_1, 7 bits wide
  assign not_2_out = ~xor_1_out;  // NOT_Gate not_2, 7 bits wide
  and and_1 (same[31], not_2_out[0], not_2_out[1], not_2_out[2], not_2_out[3], not_2_out[4], not_2_out[5], not_2_out[6]);

  assign same[30:0] = {31{same[31]}};
endmodule

module is_add (
  input  [6:0] opcode,
  input  [2:0] funct3,
  input  [6:0] funct7,
  output [31:0] same
);

  wire [2:0] not_4_out, xor_2_out;
  wire [6:0] not_2_out, not_3_out, xor_1_out;
  wire [6:6] not_1_out;

  not not_1 (not_1_out[6], 1'b1);
  assign not_2_out = ~funct7;  // NOT_Gate not_2, 7 bits wide
  assign xor_1_out = {not_1_out[6], 2'b11, {2{not_1_out[6]}}, 2'b11} ^ opcode;  // XOR_Gate xor_1, 7 bits wide
  assign xor_2_out = funct3 ^ {3{not_1_out[6]}};  // XOR_Gate xor_2, 3 bits wide
  assign not_3_out = ~xor_1_out;  // NOT_Gate not_3, 7 bits wide
  assign not_4_out = ~xor_2_out;  // NOT_Gate not_4, 3 bits wide
  and and_1 (same[31], not_3_out[0], not_3_out[1], not_3_out[2], not_3_out[3], not_3_out[4], not_4_out[0], not_4_out[1], not_2_out[4], not_4_out[2], not_3_out[5], not_3_out[6], not_2_out[0], not_2_out[1], not_2_out[2], not_2_out[3], not_2_out[5], not_2_out[6]);

  assign same[30:0] = {31{same[31]}};
endmodule

module is_lw (
  input  [6:0] opcode,
  input  [2:0] funct3,
  output [31:0] same
);

  wire [2:0] not_3_out, xor_2_out;
  wire [6:0] not_2_out, xor_1_out;
  wire [6:6] not_1_out;

  not not_1 (not_1_out[6], 1'b1);
  assign xor_1_out = {{5{not_1_out[6]}}, 2'b11} ^ opcode;  // XOR_Gate xor_1, 7 bits wide
  assign xor_2_out = funct3 ^ {not_1_out[6], 1'b1, not_1_out[6]};  // XOR_Gate xor_2, 3 bits wide
  assign not_2_out = ~xor_1_out;  // NOT_Gate not_2, 7 bits wide
  assign not_3_out = ~xor_2_out;  // NOT_Gate not_3, 3 bits wide
  and and_1 (same[31], not_2_out[0], not_2_out[1], not_2_out[2], not_2_out[3], not_2_out[4], not_2_out[5], not_2_out[6], not_3_out[0], not_3_out[1], not_3_out[2]);

  assign same[30:0] = {31{same[31]}};
endmodule

module is_lbu (
  input  [6:0] opcode,
  input  [2:0] funct3,
  output [31:0] same
);

  wire [2:0] not_3_out, xor_2_out;
  wire [6:0] not_2_out, xor_1_out;
  wire [6:6] not_1_out;

  not not_1 (not_1_out[6], 1'b1);
  assign xor_1_out = {{5{not_1_out[6]}}, 2'b11} ^ opcode;  // XOR_Gate xor_1, 7 bits wide
  assign xor_2_out = funct3 ^ {1'b1, {2{not_1_out[6]}}};  // XOR_Gate xor_2, 3 bits wide
  assign not_2_out = ~xor_1_out;  // NOT_Gate not_2, 7 bits wide
  assign not_3_out = ~xor_2_out;  // NOT_Gate not_3, 3 bits wide
  and and_1 (same[31], not_2_out[0], not_2_out[1], not_2_out[2], not_2_out[3], not_2_out[4], not_2_out[5], not_2_out[6], not_3_out[0], not_3_out[1], not_3_out[2]);

  assign same[30:0] = {31{same[31]}};
endmodule

module is_sw (
  input  [6:0] opcode,
  input  [2:0] funct3,
  output [31:0] same
);

  wire [2:0] not_3_out, xor_2_out;
  wire [6:0] not_2_out, xor_1_out;
  wire [6:6] not_1_out;

  not not_1 (not_1_out[6], 1'b1);
  assign xor_1_out = {not_1_out[6], 1'b1, {3{not_1_out[6]}}, 2'b11} ^ opcode;  // XOR_Gate xor_1, 7 bits wide
  assign xor_2_out = funct3 ^ {not_1_out[6], 1'b1, not_1_out[6]};  // XOR_Gate xor_2, 3 bits wide
  assign not_2_out = ~xor_1_out;  // NOT_Gate not_2, 7 bits wide
  assign not_3_out = ~xor_2_out;  // NOT_Gate not_3, 3 bits wide
  and and_1 (same[31], not_2_out[0], not_2_out[1], not_2_out[2], not_2_out[3], not_2_out[4], not_2_out[5], not_2_out[6], not_3_out[0], not_3_out[1], not_3_out[2]);

  assign same[30:0] = {31{same[31]}};
endmodule

module is_sb (
  input  [6:0] opcode,
  input  [2:0] funct3,
  output [31:0] same
);

  wire [2:0] not_3_out, xor_2_out;
  wire [6:0] not_2_out, xor_1_out;
  wire [6:6] not_1_out;

  not not_1 (not_1_out[6], 1'b1);
  assign xor_1_out = {not_1_out[6], 1'b1, {3{not_1_out[6]}}, 2'b11} ^ opcode;  // XOR_Gate xor_1, 7 bits wide
  assign xor_2_out = funct3 ^ {3{not_1_out[6]}};  // XOR_Gate xor_2, 3 bits wide
  assign not_2_out = ~xor_1_out;  // NOT_Gate not_2, 7 bits wide
  assign not_3_out = ~xor_2_out;  // NOT_Gate not_3, 3 bits wide
  and and_1 (same[31], not_2_out[0], not_2_out[1], not_2_out[2], not_2_out[3], not_2_out[4], not_2_out[5], not_2_out[6], not_3_out[0], not_3_out[1], not_3_out[2]);

  assign same[30:0] = {31{same[31]}};
endmodule

module decode (
  input  [31:0] instruction,
  output [4:0] rs1,
  output [4:0] rs2,
  output [4:0] rd,
  output [31:0] addi,
  output [31:0] jalr,
  output [31:0] lui,
  output [31:0] add,
  output [31:0] lw,
  output [31:0] lbu,
  output [31:0] sw,
  output [31:0] sb,
  output [11:0] I_type_imm,
  output [19:0] U_type_imm,
  output [11:0] S_type_imm
);

  is_addi addi_body (.opcode(instruction[6:0]), .funct3(instruction[14:12]), .same(addi));
  is_jalr jalr_body (.opcode(instruction[6:0]), .funct3(instruction[14:12]), .same(jalr));
  is_lui lui_body (.opcode(instruction[6:0]), .same(lui));
  is_add add_body (.opcode(instruction[6:0]), .funct3(instruction[14:12]), .funct7(instruction[31:25]), .same(add));
  is_lw lw_body (.opcode(instruction[6:0]), .funct3(instruction[14:12]), .same(lw));
  is_lbu lbu_body (.opcode(instruction[6:0]), .funct3(instruction[14:12]), .same(lbu));
  is_sw sw_body (.opcode(instruction[6:0]), .funct3(instruction[14:12]), .same(sw));
  is_sb sb_body (.opcode(instruction[6:0]), .funct3(instruction[14:12]), .same(sb));

  assign I_type_imm = instruction[31:20];
  assign rd = instruction[11:7];
  assign rs1 = instruction[19:15];
  assign rs2 = instruction[24:20];
  assign S_type_imm = {instruction[31:25], instruction[11:7]};
  assign U_type_imm = instruction[31:12];
endmodule

module \logic  (
  input  [31:0] pc,
  input  [11:0] S_type_imm,
  input  [19:0] U_type_imm,
  input  [11:0] I_type_imm,
  input  [31:0] rs1_data,
  input  [31:0] rs2_data,
  input  [31:0] addi,
  input  [31:0] jalr,
  input  [31:0] lui,
  input  [31:0] add,
  input  [31:0] lw,
  input  [31:0] mread_data,
  input  [31:0] sw,
  input  [31:0] lbu,
  input  [31:0] sb,
  output [31:0] out_data,
  output set,
  output [31:0] set_data,
  output [31:0] memory_addr,
  output write,
  output [31:0] mwrite_data,
  output [23:0] vga_data,
  output is_sb,
  output wenable
);

  wire sw_body_write;
  wire [31:0] add_body_out_data, addi_body_out_data, jalr_body_out_data, lbu_body_out_data,
       lui_body_out_data, lw_body_mread_addr, lw_body_out_data, sb_body_mwrite_data, sw_body_mwrite_addr,
       sw_body_mwrite_data;

  function_addi addi_body (.addi(addi), .I_type_imm(I_type_imm), .rs1_data(rs1_data), .out_data(addi_body_out_data));
  function_jalr jalr_body (
    .jalr(jalr), .pc(pc), .rs1_data(rs1_data), .I_type_imm(I_type_imm), .out_data(jalr_body_out_data),
    .set_data(set_data), .set(set));
  fuction_lui lui_body (.lui(lui), .U_type_imm(U_type_imm), .out_data(lui_body_out_data));
  function_add add_body (.add(add), .rs1_data(rs1_data), .rs2_data(rs2_data), .out_data(add_body_out_data));
  function_lw lw_body (
    .lw(lw), .I_type_imm(I_type_imm), .rs1_data(rs1_data), .mread_data(mread_data),
    .mread_addr(lw_body_mread_addr), .out_data(lw_body_out_data));
  function_sw sw_body (
    .sw(sw), .rs1_data(rs1_data), .S_type_imm(S_type_imm), .rs2_data(rs2_data), .write(sw_body_write),
    .mwrite_addr(sw_body_mwrite_addr), .mwrite_data(sw_body_mwrite_data));
  function_lbu lbu_body (
    .lbu(lbu), .memory_addr(lw_body_mread_addr), .mread_data(mread_data), .out_data(lbu_body_out_data));
  function_sb sb_body (.sb(sb), .rs2_data(rs2_data), .write(is_sb), .mwrite_data(sb_body_mwrite_data));
  or or_1 (write, sw_body_write, is_sb);
  assign out_data = addi_body_out_data | lbu_body_out_data | jalr_body_out_data | lui_body_out_data | lw_body_out_data | add_body_out_data;  // OR_Gate or_2, 32 bits wide
  assign mwrite_data = sw_body_mwrite_data | sb_body_mwrite_data;  // OR_Gate or_3, 32 bits wide
  not not_1 (wenable, write);
  Multiplexer #(.width(32)) multiplexer_1 (
    .in0(lw_body_mread_addr), .in1(sw_body_mwrite_addr), .out(memory_addr), .sel(write));

  assign vga_data = mwrite_data[23:0];
endmodule

module function_addi (
  input  [31:0] addi,
  input  [11:0] I_type_imm,
  input  [31:0] rs1_data,
  output [31:0] out_data
);

  wire [31:0] adder_1_out, bit_extender_1_out;

  assign bit_extender_1_out = {{20{I_type_imm[11]}}, I_type_imm};  // Bit_Extender bit_extender_1
  Adder #(.width(32)) adder_1 (.a(bit_extender_1_out), .b(rs1_data), .out(adder_1_out));  // open: cin, cout
  assign out_data = addi & adder_1_out;  // AND_Gate and_1, 32 bits wide
endmodule

module function_jalr (
  input  [31:0] jalr,
  input  [31:0] pc,
  input  [31:0] rs1_data,
  input  [11:0] I_type_imm,
  output [31:0] out_data,
  output [31:0] set_data,
  output set
);

  wire [31:0] adder_1_out, bit_extender_1_out;

  assign bit_extender_1_out = {{20{I_type_imm[11]}}, I_type_imm};  // Bit_Extender bit_extender_1
  Adder #(.width(32)) adder_1 (.a(pc), .b(32'h4), .out(adder_1_out));  // open: cin, cout
  Adder #(.width(32)) adder_2 (.a(rs1_data), .b(bit_extender_1_out), .out(set_data));  // open: cin, cout
  assign out_data = jalr & adder_1_out;  // AND_Gate and_1, 32 bits wide

  assign set = jalr[0];
endmodule

module fuction_lui (
  input  [31:0] lui,
  input  [19:0] U_type_imm,
  output [31:0] out_data
);

  assign out_data = lui & {U_type_imm, {12{1'b0}}};  // AND_Gate and_1, 32 bits wide
endmodule

module function_add (
  input  [31:0] add,
  input  [31:0] rs1_data,
  input  [31:0] rs2_data,
  output [31:0] out_data
);

  wire [31:0] adder_1_out;

  Adder #(.width(32)) adder_1 (.a(rs1_data), .b(rs2_data), .out(adder_1_out));  // open: cin, cout
  assign out_data = add & adder_1_out;  // AND_Gate and_1, 32 bits wide
endmodule

module function_lw (
  input  [31:0] lw,
  input  [11:0] I_type_imm,
  input  [31:0] rs1_data,
  input  [31:0] mread_data,
  output [31:0] mread_addr,
  output [31:0] out_data
);

  wire [31:0] bit_extender_1_out;

  assign bit_extender_1_out = {{20{I_type_imm[11]}}, I_type_imm};  // Bit_Extender bit_extender_1
  assign out_data = lw & mread_data;  // AND_Gate and_1, 32 bits wide
  Adder #(.width(32)) adder_1 (.a(bit_extender_1_out), .b(rs1_data), .out(mread_addr));  // open: cin, cout
endmodule

module R_O_M (
  input  [31:0] pc,
  output [31:0] instruction
);

  ROM #(.addrWidth(20), .dataWidth(32)) rom_1 (.addr(pc[21:2]), .data(instruction));

  // Notes on the sheet:
  //   contents of rom_1 (hex, n*v repeats v):
  //   413 93137 10113 10b7 dbc08093 80e7 fe012823 fea10923 fea12423 fe914203 fe4109a3 ff012783 f787b3
  //   f787b3 4b6b7 f0068693 fdc10113 d787b3 10000713 f12423 10593 100793 b00513 2112023 12023 12223 e12623
  //   e12823 f10a23 10b7 a8408093 80e7 2012083 2410113 8067 ff410113 112423 10b7 a7c08093 80e7 513 1800093
  //   80e7 812083 513 c10113 8067 852583 feb12823 fe812e23 3437 a0840413 ff014183 3401b3 1c183 ff114203
  //   440233 24203 4181b3 ff214203 440233 24203 4181b3 ff314203 440233 24203 4181b3 3237 a0020213 320233
  //   24203 ffc12403 420233 420233 410233 11b7 85c18193 fe312823 14800193 fe312623 fec22203 20067 1052703
  //   52683 452783 fe810113 e12423 112a23 fed12823 fef12623 13737 c0070713 fe012223 ff314203 fe4102a3
  //   fef14203 fe410223 fe412203 470233 24203 fe4105a3 ff214203 fe4102a3 fee14203 fe410223 fe412203 470233
  //   24203 fe410523 ff114203 fe4102a3 fed14203 fe410223 fe412203 470233 24203 fe4104a3 ff014203 fe4102a3
  //   fec14203 fe410223 fe412203 470233 24203 fe410423 fe812703 c52603 fee12823 fe812e23 3437 a0840413
  //   ff014183 3401b3 1c183 ff114203 440233 24203 4181b3 ff214203 440233 24203 4181b3 ff314203 440233
  //   24203 4181b3 3237 a0020213 320233 24203 ffc12403 420233 420233 410233 66800193 fe312823 28000193
  //   fe312623 fec22203 20067 c68733 10000513 fe812e23 fe912c23 fee12823 50413 ff012483 fe812423 feb14183
  //   3181b3 fe312423 fe914183 3181b3 fe912423 feb14203 420233 fe412423 fe914203 4181b3 3181b3 fe312a23
  //   fe912423 33237 b0020213 feb14183 4181b3 1c183 fe3103a3 fea14183 4181b3 1c183 fe310323 fe914183
  //   4181b3 1c183 fe3102a3 fe814183 4181b3 1c183 fe310223 ff412183 fe412203 440233 120213 fe412423
  //   feb14203 420233 fe412423 fe914203 4181b3 3237 b0820213 320233 ff812483 ffc12403 24203 420233 420233
  //   410233 11b7 86018193 fe312823 38800193 fe312623 fec22203 20067 812703 10000513 812823 e78733
  //   fe812e23 fe912c23 fee12823 50413 ff012483 fe812423 feb14183 3181b3 fe312423 fe914183 3181b3 fe912423
  //   feb14203 420233 fe412423 fe914203 4181b3 3181b3 fe312a23 fe912423 33237 b0020213 feb14183 4181b3
  //   1c183 fe3103a3 fea14183 4181b3 1c183 fe310323 fe914183 4181b3 1c183 fe3102a3 fe814183 4181b3 1c183
  //   fe310223 ff412183 fe412203 440233 120213 fe412423 feb14203 420233 fe412423 fe914203 4181b3 3237
  //   b0820213 320233 ff812483 ffc12403 24203 420233 420233 410233 11b7 86418193 fe312823 49800193
  //   fe312623 fec22203 20067 8*f787b3 d787b3 f787b3 f787b3 20000437 f40433 812783 c60633 c60633 fef12423
  //   feb14183 3181b3 fe312423 fe914183 fff78213 fe412423 feb14203 420233 fe412423 fe914203 4181b3 3237
  //   b1820213 418233 24203 420233 420233 410233 65800193 fe312823 53c00193 fe312623 fec22203 20067 912623
  //   493 40513 c12223 b12023 10b7 de008093 80e7 12583 412603 812783 148493 40040413 c585b3 fef12823
  //   fe912623 fe812e23 fe912c23 4b437 d0040413 ff014183 340233 100193 320023 fec14183 3401b3 18023 24183
  //   ff114483 940233 100493 920023 fed14483 9404b3 48023 24483 9181b3 ff214483 940233 100493 920023
  //   fee14483 9404b3 48023 24483 9181b3 ff314483 940233 100493 920023 fef14483 9404b3 48023 24483 9181b3
  //   3237 a0020213 320233 24203 ff812483 ffc12403 420233 420233 410233 65400193 fe312823 54400193
  //   fe312623 fec22203 20067 c12483 1012403 1412083 1810113 8067 10000713 fec12823 fee12623 fe812e23
  //   fe912c23 4b437 d0040413 ff014183 340233 100193 320023 fec14183 3401b3 18023 24183 ff114483 940233
  //   100493 920023 fed14483 9404b3 48023 24483 9181b3 ff214483 940233 100493 920023 fee14483 9404b3 48023
  //   24483 9181b3 ff314483 940233 100493 920023 fef14483 9404b3 48023 24483 9181b3 3237 a0020213 320233
  //   24203 ff812483 ffc12403 420233 420233 410233 74c00193 fe312823 28000193 fe312623 fec22203 20067
  //   812703 fee12823 fec12623 fe812e23 fe912c23 4b437 d0040413 ff014183 340233 100193 320023 fec14183
  //   3401b3 18023 24183 ff114483 940233 100493 920023 fed14483 9404b3 48023 24483 9181b3 ff214483 940233
  //   100493 920023 fee14483 9404b3 48023 24483 9181b3 ff314483 940233 100493 920023 fef14483 9404b3 48023
  //   24483 9181b3 3237 a0020213 320233 24203 ff812483 ffc12403 420233 420233 410233 11b7 83418193
  //   fe312823 38800193 fe312623 fec22203 20067 1412083 40637 20000537 1810113 1237 de020213 20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
endmodule

module R_A_M (
  input  [31:0] memory_addr,
  input  write,
  input  clock,
  input  [31:0] mwrite_data,
  input  is_sb,
  input  mem,
  output [31:0] mread_data
);

  wire and_1_out, decoder_1_out0, decoder_1_out1, decoder_1_out2, decoder_1_out3, not_1_out, or_1_out,
       or_2_out, or_3_out, or_4_out;
  wire [31:0] multiplexer_1_out, multiplexer_2_out;

  and and_1 (and_1_out, write, mem);
  not not_1 (not_1_out, is_sb);
  Decoder #(.enable("false"), .select(2)) decoder_1 (
    .out0(decoder_1_out0), .out1(decoder_1_out1), .out2(decoder_1_out2), .out3(decoder_1_out3),
    .sel(memory_addr[1:0]));
  or or_1 (or_1_out, decoder_1_out0, not_1_out);
  or or_2 (or_2_out, decoder_1_out1, not_1_out);
  or or_3 (or_3_out, decoder_1_out2, not_1_out);
  or or_4 (or_4_out, decoder_1_out3, not_1_out);
  Multiplexer #(.select(2), .width(32)) multiplexer_1 (
    .in0(mwrite_data), .in1({{16{1'b0}}, mwrite_data[7:0], {8{1'b0}}}),
    .in2({{8{1'b0}}, mwrite_data[7:0], {16{1'b0}}}), .in3({mwrite_data[7:0], {24{1'b0}}}),
    .out(multiplexer_1_out), .sel(memory_addr[1:0]));
  Multiplexer #(.width(32)) multiplexer_2 (
    .in0(multiplexer_1_out), .in1(mwrite_data), .out(multiplexer_2_out), .sel(not_1_out));
  RAM #(.addrWidth(20), .asyncread("true"), .byteenables("byteEnables"), .dataWidth(32), .\type ("nonvolatile")) ram_1 (
    .addr(memory_addr[21:2]), .we(and_1_out), .oe(1'b1), .clk(clock), .din(multiplexer_2_out),
    .dout(mread_data), .be3(or_4_out), .be2(or_3_out), .be1(or_2_out), .be0(or_1_out));
endmodule

module function_sw (
  input  [31:0] sw,
  input  [31:0] rs1_data,
  input  [11:0] S_type_imm,
  input  [31:0] rs2_data,
  output write,
  output [31:0] mwrite_addr,
  output [31:0] mwrite_data
);

  wire [31:0] bit_extender_1_out;

  assign bit_extender_1_out = {{20{S_type_imm[11]}}, S_type_imm};  // Bit_Extender bit_extender_1
  Adder #(.width(32)) adder_1 (.a(rs1_data), .b(bit_extender_1_out), .out(mwrite_addr));  // open: cin, cout
  assign mwrite_data = rs2_data;  // AND_Gate and_1, 32 bits wide AND_Gate

  assign write = sw[0];
endmodule

module function_lbu (
  input  [31:0] lbu,
  input  [31:0] memory_addr,
  input  [31:0] mread_data,
  output [31:0] out_data
);

  wire [7:0] multiplexer_1_out;

  Multiplexer #(.select(2), .width(8)) multiplexer_1 (
    .in0(mread_data[7:0]), .in1(mread_data[15:8]), .in2(mread_data[23:16]), .in3(mread_data[31:24]),
    .out(multiplexer_1_out), .sel(memory_addr[1:0]));
  assign out_data = lbu & {{24{1'b0}}, multiplexer_1_out};  // AND_Gate and_1, 32 bits wide
endmodule

module function_sb (
  input  [31:0] sb,
  input  [31:0] rs2_data,
  output write,
  output [31:0] mwrite_data
);

  assign mwrite_data = sb & {{24{1'b0}}, rs2_data[7:0]};  // AND_Gate and_1, 32 bits wide

  assign write = sb[0];
endmodule

module is_VGA (
  input  [31:0] addr,
  output vga,
  output mem
);

  wire comparator_1_eq, comparator_1_gt, comparator_2_lt, or_1_out;

  Comparator #(.width(32)) comparator_1 (
    .a(addr), .b(32'h20000000), .gt(comparator_1_gt), .eq(comparator_1_eq));  // open: lt
  Comparator #(.width(32)) comparator_2 (.a(addr), .b(32'h20040000), .lt(comparator_2_lt));  // open: gt, eq
  or or_1 (or_1_out, comparator_1_gt, comparator_1_eq);
  and and_1 (vga, or_1_out, comparator_2_lt);
  not not_1 (mem, vga);
endmodule

module coordinates (
  input  [31:0] addr,
  output [7:0] y,
  output [7:0] x
);

  wire [31:0] divider_1_rem, subtractor_1_out;
  wire [31:8] divider_1_out, divider_2_out;

  Subtractor #(.width(32)) subtractor_1 (.a(addr), .b(32'h20000000), .out(subtractor_1_out));  // open: bin, bout
  Divider #(.width(32)) divider_1 (
    .a(subtractor_1_out), .b(32'h400), .out({divider_1_out, y}), .rem(divider_1_rem));  // open: upper
  Divider #(.width(32)) divider_2 (.a(divider_1_rem), .b(32'h4), .out({divider_2_out, x}));  // open: upper, rem
endmodule
